// Logisim project ALU.circ as structural Verilog: 1 circuit, main circuit main
module main (
  input  A0,
  input  A1,
  input  A2,
  input  A3,
  input  CS2,
  input  CS1,
  input  CS0,
  input  B0,
  input  B1,
  input  B2,
  input  B3,
  output F0,
  output F1,
  output F2,
  output F3,
  output C,
  output Z,
  output S,
  output V
);

  wire main_1__6__s2, main_1_cout, main_2__6__s2, main_2_cout, n7404_1__2__1y, n7404_1__4__2y,
       n7404_1__6__3y, n7404_1__8__4y, n7404_1__10__5y, n7404_1__12__6y, n7408_1__3__1y, n7408_1__6__2y,
       n7408_1__8__3y, n7408_1__11__4y, n7408_2__3__1y, n7408_2__6__2y, n7408_2__8__3y, n7408_2__11__4y,
       n7408_3__3__1y, n7432_1__3__1y, n7432_1__6__2y, n7432_1__8__3y, n7432_1__11__4y, n7432_2__3__1y,
       n7432_2__6__2y, n7432_2__8__3y, n7432_2__11__4y, n7486_1__3__1y;

  _7404 u_7404_1 (
    ._1__1A(CS2), ._2__1Y(n7404_1__2__1y), ._3__2A(CS1), ._4__2Y(n7404_1__4__2y), ._5__3A(CS0),
    ._6__3Y(n7404_1__6__3y), ._7__GND(1'b0), ._14__Vcc(1'b1), ._13__6A(n7432_2__11__4y),
    ._12__6Y(n7404_1__12__6y), ._11__5A(n7432_2__8__3y), ._10__5Y(n7404_1__10__5y), ._9__4A(n7408_2__3__1y),
    ._8__4Y(n7404_1__8__4y));
  _7408 u_7408_1 (
    ._1__1A(B0), ._2__1B(n7432_2__3__1y), ._3__1Y(n7408_1__3__1y), ._4__2A(B1), ._5__2B(n7432_2__3__1y),
    ._6__2Y(n7408_1__6__2y), ._7__GND(1'b0), ._14__Vcc(1'b1), ._13__4B(B2), ._12__4A(n7432_2__3__1y),
    ._11__4Y(n7408_1__11__4y), ._10__3B(n7432_2__3__1y), ._9__3A(B3), ._8__3Y(n7408_1__8__3y));
  _7408 u_7408_2 (
    ._1__1A(CS2), ._2__1B(n7404_1__4__2y), ._3__1Y(n7408_2__3__1y), ._4__2A(n7404_1__6__3y),
    ._5__2B(n7404_1__8__4y), ._6__2Y(n7408_2__6__2y), ._7__GND(1'b0), ._14__Vcc(1'b1),
    ._13__4B(n7408_2__3__1y), ._12__4A(n7432_2__6__2y), ._11__4Y(n7408_2__11__4y), ._10__3B(n7404_1__2__1y),
    ._9__3A(CS0), ._8__3Y(n7408_2__8__3y));
  _7432 u_7432_1 (
    ._1__1A(n7408_2__6__2y), ._2__1B(n7408_1__3__1y), ._3__1Y(n7432_1__3__1y), ._4__2A(n7408_2__6__2y),
    ._5__2B(n7408_1__6__2y), ._6__2Y(n7432_1__6__2y), ._7__GND(1'b0), ._14__Vcc(1'b1),
    ._13__4B(n7408_2__6__2y), ._12__4A(n7408_1__11__4y), ._11__4Y(n7432_1__11__4y), ._10__3B(n7408_2__6__2y),
    ._9__3A(n7408_1__8__3y), ._8__3Y(n7432_1__8__3y));
  _7432 u_7432_2 (
    ._1__1A(CS2), ._2__1B(CS1), ._3__1Y(n7432_2__3__1y), ._4__2A(n7408_2__8__3y), ._5__2B(n7404_1__4__2y),
    ._6__2Y(n7432_2__6__2y), ._7__GND(1'b0), ._14__Vcc(1'b1), ._13__4B(F0), ._12__4A(F1),
    ._11__4Y(n7432_2__11__4y), ._10__3B(F3), ._9__3A(F2), ._8__3Y(n7432_2__8__3y));
  adderseparate_main main_1 (
    ._1__A4(A1), ._3__A3(n7432_2__6__2y), ._4__B3(main_1__6__s2), ._5__Vcc(1'b1), ._6__S2(main_1__6__s2),
    ._7__B2(1'b0), ._8__A2(1'b0), ._16__B4(n7432_1__6__2y), ._15__S4(F1), .Cout(main_1_cout),
    ._13__Cin(n7408_2__11__4y), ._12__GND(1'b0), ._11__B1(n7432_1__3__1y), ._10__A1(A0), ._9__S1(F0));  // open: _2__S3
  adderseparate_main main_2 (
    ._1__A4(A3), ._3__A3(n7432_2__6__2y), ._4__B3(main_2__6__s2), ._5__Vcc(1'b1), ._6__S2(main_2__6__s2),
    ._7__B2(1'b0), ._8__A2(1'b0), ._16__B4(n7432_1__8__3y), ._15__S4(F3), .Cout(main_2_cout),
    ._13__Cin(n7408_3__3__1y), ._12__GND(1'b0), ._11__B1(n7432_1__11__4y), ._10__A1(A2), ._9__S1(F2));  // open: _2__S3
  _7408 u_7408_3 (
    ._1__1A(main_1_cout), ._2__1B(n7432_2__6__2y), ._3__1Y(n7408_3__3__1y), ._4__2A(main_2_cout),
    ._5__2B(n7432_2__6__2y), ._6__2Y(C), ._7__GND(1'b0), ._14__Vcc(1'b1), ._13__4B(n7404_1__12__6y),
    ._12__4A(n7404_1__10__5y), ._11__4Y(Z), ._10__3B(n7486_1__3__1y), ._9__3A(n7432_2__6__2y), ._8__3Y(V));
  _7486 u_7486_1 (
    ._1__1A(main_2_cout), ._2__1B(main_2__6__s2), ._3__1Y(n7486_1__3__1y), ._7__GND(1'b0), ._14__Vcc(1'b1));  // open: _4__2A, _5__2B, _6__2Y, _13__4B, _12__4A, _11__4Y, _10__3B, _9__3A, _8__3Y

  assign S = F3;

  // Notes on the sheet:
  //   A/L
  //   Cin
  //   Y0
  //   Y1
  //   Y2
  //   Y3
endmodule
