// Logisim project B1_Group5_4bit_MIPS.circ as structural Verilog: 11 circuits, main circuit InstructionMemory
// InsMem
module InstructionMemory (
  input  [7:0] PC,
  output [3:0] Dst_Reg_Shamt_Addr__Immdt__0_3,
  output [3:0] Src_Reg_2_Dst_Reg__4_7,
  output [3:0] Src_Reg_1__8_11,
  output [3:0] Opcode__12_15
);

  ROM #(.dataWidth(16)) rom_1 (
    .addr(PC), .data({Opcode__12_15, Src_Reg_1__8_11, Src_Reg_2_Dst_Reg__4_7, Dst_Reg_Shamt_Addr__Immdt__0_3}));  // open: sel

  // Notes on the sheet:
  //   contents of rom_1 (hex, n*v repeats v):
  //   706c 7023 7035 3231 3134 7452 1323 2222 4441 a421 260 9441 d422 c241 5153 230 7120 1620 4661 7320
  //   1620 4661 f115 7661 d610 6336 d322 1620 4661 7661 d630 8333 7661 d630 260 e311 4113 100
endmodule

// alu0
module ALU4bit (
  input  [2:0] ALUop,
  input  [3:0] A,
  input  [3:0] B,
  output [3:0] Out,
  output Zero
);

  wire or1bit4x1_1_output;
  wire [3:0] adder4bit_1_dataout, adder4bit_2_dataout, and_1_out, leftshifter_1_out, mux4bit2x1_1_dataout,
       mux4bit2x1_2_dataout, mux4bit2x1_3_dataout, mux4bit2x1_4_dataout, mux4bit2x1_5_dataout,
       mux4bit2x1_7_dataout, nor_1_out, not4bit_1_output, or_1_out, rightshifter_1_out;

  Adder4bit adder4bit_1 (.Data0(A), .Data1(B), .Cin(1'b0), .DataOut(adder4bit_1_dataout));  // open: Cout
  NOT4bit not4bit_1 (.Input(B), .Output(not4bit_1_output));
  Adder4bit adder4bit_2 (.Data0(A), .Data1(not4bit_1_output), .Cin(1'b1), .DataOut(adder4bit_2_dataout));  // open: Cout
  assign or_1_out = A | B;  // OR_Gate or_1, 4 bits wide
  assign and_1_out = A & B;  // AND_Gate and_1, 4 bits wide
  assign nor_1_out = ~(A | B);  // NOR_Gate nor_1, 4 bits wide
  LeftShifter leftshifter_1 (.in(A), .shamt(B), .out(leftshifter_1_out));
  RightShifter rightshifter_1 (.in(A), .shamt(B), .out(rightshifter_1_out));
  MUX4bit2x1 mux4bit2x1_1 (
    .S(ALUop[0]), .Data0(adder4bit_1_dataout), .Data1(adder4bit_2_dataout), .DataOut(mux4bit2x1_1_dataout));
  MUX4bit2x1 mux4bit2x1_2 (.S(ALUop[0]), .Data0(or_1_out), .Data1(and_1_out), .DataOut(mux4bit2x1_2_dataout));
  MUX4bit2x1 mux4bit2x1_3 (.S(ALUop[0]), .Data0(nor_1_out), .Data1(leftshifter_1_out), .DataOut(mux4bit2x1_3_dataout));
  MUX4bit2x1 mux4bit2x1_4 (.S(ALUop[0]), .Data0(rightshifter_1_out), .Data1(4'b0000), .DataOut(mux4bit2x1_4_dataout));
  MUX4bit2x1 mux4bit2x1_5 (
    .S(ALUop[1]), .Data0(mux4bit2x1_1_dataout), .Data1(mux4bit2x1_2_dataout), .DataOut(mux4bit2x1_5_dataout));
  MUX4bit2x1 mux4bit2x1_6 (.S(ALUop[2]), .Data0(mux4bit2x1_5_dataout), .Data1(mux4bit2x1_7_dataout), .DataOut(Out));
  MUX4bit2x1 mux4bit2x1_7 (
    .S(ALUop[1]), .Data0(mux4bit2x1_3_dataout), .Data1(mux4bit2x1_4_dataout), .DataOut(mux4bit2x1_7_dataout));
  NOT1bit not1bit_1 (.Input(or1bit4x1_1_output), .Output(Zero));
  OR1BIT4X1 or1bit4x1_1 (.Input_A(Out), .Output(or1bit4x1_1_output));

  // Notes on the sheet:
  //   000 Add
  //   001 Sub
  //   010 And
  //   011 Or
  //   100 Nor
  //   101 SL
  //   110 SR
  //   111 Zero
endmodule

module Control (
  input  [3:0] opCode,
  output jump,
  output RegDst,
  output RegWrite,
  output MemRead,
  output MemWrite,
  output MemtoReg,
  output beq,
  output bneq,
  output ALUsrc,
  output [2:0] ALUop
);

  ROM #(.addrWidth(4), .dataWidth(12)) rom_1 (
    .addr(opCode), .data({ALUop, ALUsrc, bneq, beq, MemtoReg, MemWrite, MemRead, RegWrite, RegDst, jump}),
    .sel(1'b1));

  // Notes on the sheet:
  //   contents of rom_1 (hex, n*v repeats v):
  //   1 110 b04 6 304 406 704 104 806 d04 240 206 606 12c 280 504
endmodule

// registers
module Registers (
  input  [3:0] in_zero,
  input  CLKzero,
  input  [3:0] in_t0,
  input  CLK0,
  input  [3:0] in_t1,
  input  CLK1,
  input  [3:0] in_t2,
  input  CLK2,
  input  [3:0] in_t3,
  input  CLK3,
  input  [3:0] in_t4,
  input  CLK4,
  input  [3:0] in_sp,
  input  CLKsp,
  output [3:0] zero,
  output [3:0] t0,
  output [3:0] t1,
  output [3:0] t2,
  output [3:0] t3,
  output [3:0] t4,
  output [3:0] sp
);

  wire [3:0] n7474_1__5__q1;

  _7474 u_7474_1 (
    ._2__D1(in_zero[0]), ._3__CLK1(CLKzero), ._5__Q1(n7474_1__5__q1[0]), ._7__GND(1'b0), ._14__Vcc(1'b1),
    ._12__D2(in_zero[1]), ._11__CLK2(CLKzero), ._9__Q2(n7474_1__5__q1[1]));  // open: _1__CLR1, _4__PR1, _6__nQ1, _13__CLR2, _10__PR2, _8__nQ2
  _7474 u_7474_2 (
    ._2__D1(in_zero[2]), ._3__CLK1(CLKzero), ._5__Q1(n7474_1__5__q1[2]), ._7__GND(1'b0), ._14__Vcc(1'b1),
    ._12__D2(in_zero[3]), ._11__CLK2(CLKzero), ._9__Q2(n7474_1__5__q1[3]));  // open: _1__CLR1, _4__PR1, _6__nQ1, _13__CLR2, _10__PR2, _8__nQ2
  _7474 u_7474_3 (
    ._2__D1(in_t0[0]), ._3__CLK1(CLK0), ._5__Q1(t0[0]), ._7__GND(1'b0), ._14__Vcc(1'b1), ._12__D2(in_t0[1]),
    ._11__CLK2(CLK0), ._9__Q2(t0[1]));  // open: _1__CLR1, _4__PR1, _6__nQ1, _13__CLR2, _10__PR2, _8__nQ2
  _7474 u_7474_4 (
    ._2__D1(in_t0[2]), ._3__CLK1(CLK0), ._5__Q1(t0[2]), ._7__GND(1'b0), ._14__Vcc(1'b1), ._12__D2(in_t0[3]),
    ._11__CLK2(CLK0), ._9__Q2(t0[3]));  // open: _1__CLR1, _4__PR1, _6__nQ1, _13__CLR2, _10__PR2, _8__nQ2
  _7474 u_7474_5 (
    ._2__D1(in_t1[0]), ._3__CLK1(CLK1), ._5__Q1(t1[0]), ._7__GND(1'b0), ._14__Vcc(1'b1), ._12__D2(in_t1[1]),
    ._11__CLK2(CLK1), ._9__Q2(t1[1]));  // open: _1__CLR1, _4__PR1, _6__nQ1, _13__CLR2, _10__PR2, _8__nQ2
  _7474 u_7474_6 (
    ._2__D1(in_t1[2]), ._3__CLK1(CLK1), ._5__Q1(t1[2]), ._7__GND(1'b0), ._14__Vcc(1'b1), ._12__D2(in_t1[3]),
    ._11__CLK2(CLK1), ._9__Q2(t1[3]));  // open: _1__CLR1, _4__PR1, _6__nQ1, _13__CLR2, _10__PR2, _8__nQ2
  _7474 u_7474_7 (
    ._2__D1(in_t2[0]), ._3__CLK1(CLK2), ._5__Q1(t2[0]), ._7__GND(1'b0), ._14__Vcc(1'b1), ._12__D2(in_t2[1]),
    ._11__CLK2(CLK2), ._9__Q2(t2[1]));  // open: _1__CLR1, _4__PR1, _6__nQ1, _13__CLR2, _10__PR2, _8__nQ2
  _7474 u_7474_8 (
    ._2__D1(in_t2[2]), ._3__CLK1(CLK2), ._5__Q1(t2[2]), ._7__GND(1'b0), ._14__Vcc(1'b1), ._12__D2(in_t2[3]),
    ._11__CLK2(CLK2), ._9__Q2(t2[3]));  // open: _1__CLR1, _4__PR1, _6__nQ1, _13__CLR2, _10__PR2, _8__nQ2
  _7474 u_7474_9 (
    ._2__D1(in_t3[0]), ._3__CLK1(CLK3), ._5__Q1(t3[0]), ._7__GND(1'b0), ._14__Vcc(1'b1), ._12__D2(in_t3[1]),
    ._11__CLK2(CLK3), ._9__Q2(t3[1]));  // open: _1__CLR1, _4__PR1, _6__nQ1, _13__CLR2, _10__PR2, _8__nQ2
  _7474 u_7474_10 (
    ._2__D1(in_t3[2]), ._3__CLK1(CLK3), ._5__Q1(t3[2]), ._7__GND(1'b0), ._14__Vcc(1'b1), ._12__D2(in_t3[3]),
    ._11__CLK2(CLK3), ._9__Q2(t3[3]));  // open: _1__CLR1, _4__PR1, _6__nQ1, _13__CLR2, _10__PR2, _8__nQ2
  _7474 u_7474_11 (
    ._2__D1(in_t4[0]), ._3__CLK1(CLK4), ._5__Q1(t4[0]), ._7__GND(1'b0), ._14__Vcc(1'b1), ._12__D2(in_t4[1]),
    ._11__CLK2(CLK4), ._9__Q2(t4[1]));  // open: _1__CLR1, _4__PR1, _6__nQ1, _13__CLR2, _10__PR2, _8__nQ2
  _7474 u_7474_12 (
    ._2__D1(in_t4[2]), ._3__CLK1(CLK4), ._5__Q1(t4[2]), ._7__GND(1'b0), ._14__Vcc(1'b1), ._12__D2(in_t4[3]),
    ._11__CLK2(CLK4), ._9__Q2(t4[3]));  // open: _1__CLR1, _4__PR1, _6__nQ1, _13__CLR2, _10__PR2, _8__nQ2
  _7474 u_7474_13 (
    ._2__D1(in_sp[0]), ._3__CLK1(CLKsp), ._5__Q1(sp[0]), ._7__GND(1'b0), ._14__Vcc(1'b1), ._12__D2(in_sp[1]),
    ._11__CLK2(CLKsp), ._9__Q2(sp[1]));  // open: _1__CLR1, _4__PR1, _6__nQ1, _13__CLR2, _10__PR2, _8__nQ2
  _7474 u_7474_14 (
    ._2__D1(in_sp[2]), ._3__CLK1(CLKsp), ._5__Q1(sp[2]), ._7__GND(1'b0), ._14__Vcc(1'b1), ._12__D2(in_sp[3]),
    ._11__CLK2(CLKsp), ._9__Q2(sp[3]));  // open: _1__CLR1, _4__PR1, _6__nQ1, _13__CLR2, _10__PR2, _8__nQ2

  assign zero = 4'b0000;
endmodule

// RegFile
module RegisterFile (
  input  [3:0] Reg_1_Address,
  input  [3:0] Reg_2_Address,
  input  [3:0] Write_Data,
  input  [3:0] Write_Reg_Address,
  input  RegWrite,
  input  Clk,
  output [3:0] Read_Data_1,
  output [3:0] Read_Data_2,
  output [3:0] zero,
  output [3:0] t0,
  output [3:0] t1,
  output [3:0] t2,
  output [3:0] t3,
  output [3:0] t4,
  output [3:0] sp
);

  wire decoder_1_out1, decoder_1_out2, decoder_1_out3, decoder_1_out4, decoder_1_out5, decoder_1_out6,
       n7408_1__3__1y;
  wire [2:0] mux3bit2x1_1_dataout;

  MUX3bit2x1 mux3bit2x1_1 (
    .S(n7408_1__3__1y), .Data0(3'b000), .Data1(Write_Reg_Address[2:0]), .DataOut(mux3bit2x1_1_dataout));
  _7408 u_7408_1 (
    ._1__1A(RegWrite), ._2__1B(Clk), ._3__1Y(n7408_1__3__1y), ._7__GND(1'b0), ._14__Vcc(1'b1));  // open: _4__2A, _5__2B, _6__2Y, _13__4B, _12__4A, _11__4Y, _10__3B, _9__3A, _8__3Y
  Decoder #(.select(3), .enable("false")) decoder_1 (
    .out1(decoder_1_out1), .out2(decoder_1_out2), .out3(decoder_1_out3), .out4(decoder_1_out4),
    .out5(decoder_1_out5), .out6(decoder_1_out6), .sel(mux3bit2x1_1_dataout));  // open: out0, out7
  Registers registers_1 (
    .in_t0(Write_Data), .CLK0(decoder_1_out1), .in_t1(Write_Data), .CLK1(decoder_1_out2), .in_t2(Write_Data),
    .CLK2(decoder_1_out3), .in_t3(Write_Data), .CLK3(decoder_1_out4), .in_t4(Write_Data),
    .CLK4(decoder_1_out5), .in_sp(Write_Data), .CLKsp(decoder_1_out6), .zero(zero), .t0(t0), .t1(t1),
    .t2(t2), .t3(t3), .t4(t4), .sp(sp));  // open: in_zero, CLKzero
  Multiplexer #(.select(3), .width(4), .enable("false")) multiplexer_1 (
    .in0(zero), .in1(t0), .in2(t1), .in3(t2), .in4(t3), .in5(t4), .in6(sp), .out(Read_Data_1),
    .sel(Reg_1_Address[2:0]));  // open: in7
  Multiplexer #(.select(3), .width(4), .enable("false")) multiplexer_2 (
    .in0(zero), .in1(t0), .in2(t1), .in3(t2), .in4(t3), .in5(t4), .in6(sp), .out(Read_Data_2),
    .sel(Reg_2_Address[2:0]));  // open: in7
endmodule

// DataMem
module DataMemory (
  input  [3:0] Address,
  input  [3:0] Write_Data,
  input  MemWrite,
  input  MemRead,
  input  CLK,
  output [3:0] MemData
);

  RAM #(.addrWidth(4), .dataWidth(4), .bus("separate")) ram_1 (
    .addr(Address), .din(Write_Data), .data(MemData), .str(MemWrite), .clk(CLK), .ld(MemRead));  // open: sel, clr
endmodule

// 8bitReg
module Register8bit (
  input  [7:0] in,
  input  CLK0,
  output [7:0] out
);

  _7474 u_7474_1 (
    ._2__D1(in[0]), ._3__CLK1(CLK0), ._5__Q1(out[0]), ._7__GND(1'b0), ._14__Vcc(1'b1), ._12__D2(in[1]),
    ._11__CLK2(CLK0), ._9__Q2(out[1]));  // open: _1__CLR1, _4__PR1, _6__nQ1, _13__CLR2, _10__PR2, _8__nQ2
  _7474 u_7474_2 (
    ._2__D1(in[2]), ._3__CLK1(CLK0), ._5__Q1(out[2]), ._7__GND(1'b0), ._14__Vcc(1'b1), ._12__D2(in[3]),
    ._11__CLK2(CLK0), ._9__Q2(out[3]));  // open: _1__CLR1, _4__PR1, _6__nQ1, _13__CLR2, _10__PR2, _8__nQ2
  _7474 u_7474_3 (
    ._2__D1(in[4]), ._3__CLK1(CLK0), ._5__Q1(out[4]), ._7__GND(1'b0), ._14__Vcc(1'b1), ._12__D2(in[5]),
    ._11__CLK2(CLK0), ._9__Q2(out[5]));  // open: _1__CLR1, _4__PR1, _6__nQ1, _13__CLR2, _10__PR2, _8__nQ2
  _7474 u_7474_4 (
    ._2__D1(in[6]), ._3__CLK1(CLK0), ._5__Q1(out[6]), ._7__GND(1'b0), ._14__Vcc(1'b1), ._12__D2(in[7]),
    ._11__CLK2(CLK0), ._9__Q2(out[7]));  // open: _1__CLR1, _4__PR1, _6__nQ1, _13__CLR2, _10__PR2, _8__nQ2
endmodule

// ALU2
module ALUencapsulated (
  input  beq,
  input  bneq,
  input  [2:0] ALUop,
  input  [3:0] Read_Data_1,
  input  [3:0] Read_Data_2,
  output bsel,
  output [3:0] out
);

  wire alu4bit_1_zero, n7404_1__2__1y, n7408_1__3__1y, n7408_1__6__2y;

  ALU4bit alu4bit_1 (.ALUop(ALUop), .A(Read_Data_1), .B(Read_Data_2), .Out(out), .Zero(alu4bit_1_zero));
  _7408 u_7408_1 (
    ._1__1A(beq), ._2__1B(alu4bit_1_zero), ._3__1Y(n7408_1__3__1y), ._4__2A(bneq), ._5__2B(n7404_1__2__1y),
    ._6__2Y(n7408_1__6__2y), ._7__GND(1'b0), ._14__Vcc(1'b1));  // open: _13__4B, _12__4A, _11__4Y, _10__3B, _9__3A, _8__3Y
  _7404 u_7404_1 (
    ._1__1A(alu4bit_1_zero), ._2__1Y(n7404_1__2__1y), ._7__GND(1'b0), ._14__Vcc(1'b1));  // open: _3__2A, _4__2Y, _5__3A, _6__3Y, _13__6A, _12__6Y, _11__5A, _10__5Y, _9__4A, _8__4Y
  _7432 u_7432_1 (
    ._1__1A(n7408_1__3__1y), ._2__1B(n7408_1__6__2y), ._3__1Y(bsel), ._7__GND(1'b0), ._14__Vcc(1'b1));  // open: _4__2A, _5__2B, _6__2Y, _13__4B, _12__4A, _11__4Y, _10__3B, _9__3A, _8__3Y
endmodule

// <<
module LeftShifter (
  input  [3:0] in,
  input  [3:0] shamt,
  output [3:0] out
);

  wire or1bit2x1_1_out_2;
  wire [3:0] mux4bit2x1_1_dataout, mux4bit2x1_2_dataout;

  MUX4bit2x1 mux4bit2x1_1 (.S(shamt[0]), .Data0(in), .Data1({in[2:0], 1'b0}), .DataOut(mux4bit2x1_1_dataout));
  OR1bit2X1 or1bit2x1_1 (.in_1(shamt[3:2]), .out_2(or1bit2x1_1_out_2));
  MUX4bit2x1 mux4bit2x1_2 (
    .S(shamt[1]), .Data0(mux4bit2x1_1_dataout), .Data1({mux4bit2x1_1_dataout[1:0], 2'b00}),
    .DataOut(mux4bit2x1_2_dataout));
  MUX4bit2x1 mux4bit2x1_3 (.S(or1bit2x1_1_out_2), .Data0(mux4bit2x1_2_dataout), .Data1(4'b0000), .DataOut(out));
endmodule

// >>
module RightShifter (
  input  [3:0] in,
  input  [3:0] shamt,
  output [3:0] out
);

  wire or1bit2x1_1_out_2;
  wire [3:0] mux4bit2x1_1_dataout, mux4bit2x1_2_dataout;

  MUX4bit2x1 mux4bit2x1_1 (.S(shamt[0]), .Data0(in), .Data1({1'b0, in[3:1]}), .DataOut(mux4bit2x1_1_dataout));
  OR1bit2X1 or1bit2x1_1 (.in_1(shamt[3:2]), .out_2(or1bit2x1_1_out_2));
  MUX4bit2x1 mux4bit2x1_2 (
    .S(shamt[1]), .Data0(mux4bit2x1_1_dataout), .Data1({2'b00, mux4bit2x1_1_dataout[3:2]}),
    .DataOut(mux4bit2x1_2_dataout));
  MUX4bit2x1 mux4bit2x1_3 (.S(or1bit2x1_1_out_2), .Data0(mux4bit2x1_2_dataout), .Data1(4'b0000), .DataOut(out));
endmodule

module MIPS (
  input  clk,
  output [3:0] readData1,
  output [3:0] readData2,
  output [3:0] writeData,
  output [7:0] nextPC,
  output [3:0] aluOut,
  output [7:0] currentPC,
  output [3:0] t0,
  output [3:0] t1,
  output [3:0] t2,
  output [3:0] t3,
  output [3:0] t4,
  output [3:0] sp
);

  wire ALU_bsel, Control_alusrc, Control_beq, Control_bneq, Control_jump, Control_memread, Control_memtoreg,
       Control_memwrite, Control_regdst, Control_regwrite, NOT1_output;
  wire [2:0] Control_aluop;
  wire [3:0] DataMem_memdata, InsMem_dst_reg_shamt_addr__immdt__0_3, InsMem_opcode__12_15,
       InsMem_src_reg_1__8_11, InsMem_src_reg_2_dst_reg__4_7, MUX1_dataout, MUX2_dataout;
  wire [7:0] Adder1_dataout, MUX4_dataout;

  Register8bit PC (.in(nextPC), .CLK0(NOT1_output), .out(currentPC));
  NOT1bit NOT1 (.Input(clk), .Output(NOT1_output));
  InstructionMemory InsMem (
    .PC(currentPC), .Dst_Reg_Shamt_Addr__Immdt__0_3(InsMem_dst_reg_shamt_addr__immdt__0_3),
    .Src_Reg_2_Dst_Reg__4_7(InsMem_src_reg_2_dst_reg__4_7), .Src_Reg_1__8_11(InsMem_src_reg_1__8_11),
    .Opcode__12_15(InsMem_opcode__12_15));
  MUX8bit2x1 MUX4 (
    .S(ALU_bsel), .Data0({8{1'b0}}),
    .Data1({{5{InsMem_dst_reg_shamt_addr__immdt__0_3[3]}}, InsMem_dst_reg_shamt_addr__immdt__0_3[2:0]}),
    .DataOut(MUX4_dataout));
  MUX8bit2x1 MUX5 (
    .S(Control_jump), .Data0(Adder1_dataout),
    .Data1({InsMem_src_reg_1__8_11, InsMem_src_reg_2_dst_reg__4_7}), .DataOut(nextPC));
  Adder8bit Adder1 (.Cin(1'b1), .Data0(currentPC), .Data1(MUX4_dataout), .DataOut(Adder1_dataout));  // open: Cout
  Control Control (
    .opCode(InsMem_opcode__12_15), .jump(Control_jump), .RegDst(Control_regdst), .RegWrite(Control_regwrite),
    .MemRead(Control_memread), .MemWrite(Control_memwrite), .MemtoReg(Control_memtoreg), .beq(Control_beq),
    .bneq(Control_bneq), .ALUsrc(Control_alusrc), .ALUop(Control_aluop));
  MUX4bit2x1 MUX1 (
    .S(Control_regdst), .Data0(InsMem_src_reg_2_dst_reg__4_7), .Data1(InsMem_dst_reg_shamt_addr__immdt__0_3),
    .DataOut(MUX1_dataout));
  RegisterFile RegFile (
    .Reg_1_Address(InsMem_src_reg_1__8_11), .Reg_2_Address(InsMem_src_reg_2_dst_reg__4_7),
    .Write_Data(writeData), .Write_Reg_Address(MUX1_dataout), .RegWrite(Control_regwrite), .Clk(clk),
    .Read_Data_1(readData1), .Read_Data_2(readData2), .t0(t0), .t1(t1), .t2(t2), .t3(t3), .t4(t4), .sp(sp));  // open: zero
  ALUencapsulated ALU (
    .beq(Control_beq), .bneq(Control_bneq), .ALUop(Control_aluop), .Read_Data_1(readData1),
    .Read_Data_2(MUX2_dataout), .bsel(ALU_bsel), .out(aluOut));
  MUX4bit2x1 MUX2 (
    .S(Control_alusrc), .Data0(readData2), .Data1(InsMem_dst_reg_shamt_addr__immdt__0_3),
    .DataOut(MUX2_dataout));
  DataMemory DataMem (
    .Address(aluOut), .Write_Data(readData2), .MemWrite(Control_memwrite), .MemRead(Control_memread),
    .CLK(clk), .MemData(DataMem_memdata));
  MUX4bit2x1 MUX3 (.S(Control_memtoreg), .Data0(aluOut), .Data1(DataMem_memdata), .DataOut(writeData));
endmodule
