// Logisim project FPA.circ as structural Verilog: 58 circuits, main circuit MUX4bit2x1
// M1
module MUX1bit2x1 (
  input  S,
  input  Data0,
  input  Data1,
  output DataOut
);

  wire n74157_1__12__y4, undriven, undriven_2;

  _74157 u_74157_1 (
    ._1__S(S), ._2__A1(Data0), ._3__B1(Data1), ._4__Y1(DataOut), ._8__GND(1'b0), ._16__Vcc(1'b1),
    ._15__G(1'b0), ._14__A4(undriven), ._13__B4(undriven_2), ._12__Y4(n74157_1__12__y4));  // open: _5__A2, _6__B2, _7__Y2, _11__A3, _10__B3, _9__Y3
endmodule

// M3
module MUX3bit2x1 (
  input  S,
  input  [2:0] Data0,
  input  [2:0] Data1,
  output [2:0] DataOut
);

  wire n74157_1__12__y4, undriven, undriven_2;

  _74157 u_74157_1 (
    ._1__S(S), ._2__A1(Data0[0]), ._3__B1(Data1[0]), ._4__Y1(DataOut[0]), ._5__A2(Data0[1]),
    ._6__B2(Data1[1]), ._7__Y2(DataOut[1]), ._8__GND(1'b0), ._16__Vcc(1'b1), ._15__G(1'b0),
    ._14__A4(undriven), ._13__B4(undriven_2), ._12__Y4(n74157_1__12__y4), ._11__A3(Data0[2]),
    ._10__B3(Data1[2]), ._9__Y3(DataOut[2]));
endmodule

// M4
module MUX4bit2x1 (
  input  S,
  input  [3:0] Data0,
  input  [3:0] Data1,
  output [3:0] DataOut
);

  _74157 u_74157_1 (
    ._1__S(S), ._2__A1(Data0[0]), ._3__B1(Data1[0]), ._4__Y1(DataOut[0]), ._5__A2(Data0[1]),
    ._6__B2(Data1[1]), ._7__Y2(DataOut[1]), ._8__GND(1'b0), ._16__Vcc(1'b1), ._15__G(1'b0),
    ._14__A4(Data0[3]), ._13__B4(Data1[3]), ._12__Y4(DataOut[3]), ._11__A3(Data0[2]), ._10__B3(Data1[2]),
    ._9__Y3(DataOut[2]));
endmodule

// M8
module MUX8bit2x1 (
  input  S,
  input  [7:0] Data0,
  input  [7:0] Data1,
  output [7:0] DataOut
);

  MUX4bit2x1 mux4bit2x1_1 (.S(S), .Data0(Data0[3:0]), .Data1(Data1[3:0]), .DataOut(DataOut[3:0]));
  MUX4bit2x1 mux4bit2x1_2 (.S(S), .Data0(Data0[7:4]), .Data1(Data1[7:4]), .DataOut(DataOut[7:4]));
endmodule

// M11
module MUX11bit2x1 (
  input  S,
  input  [10:0] Data0,
  input  [10:0] Data1,
  output [10:0] DataOut
);

  MUX4bit2x1 mux4bit2x1_1 (.S(S), .Data0(Data0[3:0]), .Data1(Data1[3:0]), .DataOut(DataOut[3:0]));
  MUX4bit2x1 mux4bit2x1_2 (.S(S), .Data0(Data0[7:4]), .Data1(Data1[7:4]), .DataOut(DataOut[7:4]));
  MUX3bit2x1 mux3bit2x1_1 (.S(S), .Data0(Data0[10:8]), .Data1(Data1[10:8]), .DataOut(DataOut[10:8]));
endmodule

// M20
module MUX20bit2x1 (
  input  S,
  input  [19:0] Data0,
  input  [19:0] Data1,
  output [19:0] DataOut
);

  MUX4bit2x1 mux4bit2x1_1 (.S(S), .Data0(Data0[3:0]), .Data1(Data1[3:0]), .DataOut(DataOut[3:0]));
  MUX4bit2x1 mux4bit2x1_2 (.S(S), .Data0(Data0[7:4]), .Data1(Data1[7:4]), .DataOut(DataOut[7:4]));
  MUX4bit2x1 mux4bit2x1_3 (.S(S), .Data0(Data0[11:8]), .Data1(Data1[11:8]), .DataOut(DataOut[11:8]));
  MUX4bit2x1 mux4bit2x1_4 (.S(S), .Data0(Data0[15:12]), .Data1(Data1[15:12]), .DataOut(DataOut[15:12]));
  MUX4bit2x1 mux4bit2x1_5 (.S(S), .Data0(Data0[19:16]), .Data1(Data1[19:16]), .DataOut(DataOut[19:16]));
endmodule

// M23
module MUX23bit2x1 (
  input  S,
  input  [22:0] Data0,
  input  [22:0] Data1,
  output [22:0] DataOut
);

  MUX4bit2x1 mux4bit2x1_1 (.S(S), .Data0(Data0[3:0]), .Data1(Data1[3:0]), .DataOut(DataOut[3:0]));
  MUX4bit2x1 mux4bit2x1_2 (.S(S), .Data0(Data0[7:4]), .Data1(Data1[7:4]), .DataOut(DataOut[7:4]));
  MUX4bit2x1 mux4bit2x1_3 (.S(S), .Data0(Data0[11:8]), .Data1(Data1[11:8]), .DataOut(DataOut[11:8]));
  MUX4bit2x1 mux4bit2x1_4 (.S(S), .Data0(Data0[15:12]), .Data1(Data1[15:12]), .DataOut(DataOut[15:12]));
  MUX3bit2x1 mux3bit2x1_1 (.S(S), .Data0(Data0[18:16]), .Data1(Data1[18:16]), .DataOut(DataOut[18:16]));
  MUX4bit2x1 mux4bit2x1_5 (.S(S), .Data0(Data0[22:19]), .Data1(Data1[22:19]), .DataOut(DataOut[22:19]));
endmodule

// M26
module MUX26bit2x1 (
  input  S,
  input  [25:0] Data0,
  input  [25:0] Data1,
  output [25:0] DataOut
);

  MUX4bit2x1 mux4bit2x1_1 (.S(S), .Data0(Data0[3:0]), .Data1(Data1[3:0]), .DataOut(DataOut[3:0]));
  MUX4bit2x1 mux4bit2x1_2 (.S(S), .Data0(Data0[7:4]), .Data1(Data1[7:4]), .DataOut(DataOut[7:4]));
  MUX4bit2x1 mux4bit2x1_3 (.S(S), .Data0(Data0[11:8]), .Data1(Data1[11:8]), .DataOut(DataOut[11:8]));
  MUX4bit2x1 mux4bit2x1_4 (.S(S), .Data0(Data0[15:12]), .Data1(Data1[15:12]), .DataOut(DataOut[15:12]));
  MUX4bit2x1 mux4bit2x1_5 (.S(S), .Data0(Data0[19:16]), .Data1(Data1[19:16]), .DataOut(DataOut[19:16]));
  MUX3bit2x1 mux3bit2x1_1 (.S(S), .Data0(Data0[22:20]), .Data1(Data1[22:20]), .DataOut(DataOut[22:20]));
  MUX3bit2x1 mux3bit2x1_2 (.S(S), .Data0(Data0[25:23]), .Data1(Data1[25:23]), .DataOut(DataOut[25:23]));
endmodule

// M29
module MUX29bit2x1 (
  input  S,
  input  [28:0] Data0,
  input  [28:0] Data1,
  output [28:0] DataOut
);

  MUX4bit2x1 mux4bit2x1_1 (.S(S), .Data0(Data0[3:0]), .Data1(Data1[3:0]), .DataOut(DataOut[3:0]));
  MUX4bit2x1 mux4bit2x1_2 (.S(S), .Data0(Data0[7:4]), .Data1(Data1[7:4]), .DataOut(DataOut[7:4]));
  MUX4bit2x1 mux4bit2x1_3 (.S(S), .Data0(Data0[11:8]), .Data1(Data1[11:8]), .DataOut(DataOut[11:8]));
  MUX4bit2x1 mux4bit2x1_4 (.S(S), .Data0(Data0[15:12]), .Data1(Data1[15:12]), .DataOut(DataOut[15:12]));
  MUX4bit2x1 mux4bit2x1_5 (.S(S), .Data0(Data0[19:16]), .Data1(Data1[19:16]), .DataOut(DataOut[19:16]));
  MUX4bit2x1 mux4bit2x1_6 (.S(S), .Data0(Data0[23:20]), .Data1(Data1[23:20]), .DataOut(DataOut[23:20]));
  MUX4bit2x1 mux4bit2x1_7 (.S(S), .Data0(Data0[27:24]), .Data1(Data1[27:24]), .DataOut(DataOut[27:24]));
  MUX1bit2x1 mux1bit2x1_1 (.S(S), .Data0(Data0[28]), .Data1(Data1[28]), .DataOut(DataOut[28]));
endmodule

// M32
module MUX32bit2x1 (
  input  S,
  input  [31:0] Data0,
  input  [31:0] Data1,
  output [31:0] DataOut
);

  MUX4bit2x1 mux4bit2x1_1 (.S(S), .Data0(Data0[3:0]), .Data1(Data1[3:0]), .DataOut(DataOut[3:0]));
  MUX4bit2x1 mux4bit2x1_2 (.S(S), .Data0(Data0[7:4]), .Data1(Data1[7:4]), .DataOut(DataOut[7:4]));
  MUX4bit2x1 mux4bit2x1_3 (.S(S), .Data0(Data0[11:8]), .Data1(Data1[11:8]), .DataOut(DataOut[11:8]));
  MUX4bit2x1 mux4bit2x1_4 (.S(S), .Data0(Data0[15:12]), .Data1(Data1[15:12]), .DataOut(DataOut[15:12]));
  MUX4bit2x1 mux4bit2x1_5 (.S(S), .Data0(Data0[19:16]), .Data1(Data1[19:16]), .DataOut(DataOut[19:16]));
  MUX4bit2x1 mux4bit2x1_6 (.S(S), .Data0(Data0[23:20]), .Data1(Data1[23:20]), .DataOut(DataOut[23:20]));
  MUX4bit2x1 mux4bit2x1_7 (.S(S), .Data0(Data0[27:24]), .Data1(Data1[27:24]), .DataOut(DataOut[27:24]));
  MUX4bit2x1 mux4bit2x1_8 (.S(S), .Data0(Data0[31:28]), .Data1(Data1[31:28]), .DataOut(DataOut[31:28]));
endmodule

// AND1
module AND1bit1X1 (
  input  in_1,
  input  in_2,
  output out_3
);

  _7408 u_7408_1 (
    ._1__1A(in_1), ._2__1B(in_2), ._3__1Y(out_3), ._7__GND(1'b0), ._14__Vcc(1'b1));  // open: _4__2A, _5__2B, _6__2Y, _13__4B, _12__4A, _11__4Y, _10__3B, _9__3A, _8__3Y
endmodule

// AND2
module AND1bit2X1 (
  input  [1:0] in_1,
  output out_2
);

  _7408 u_7408_1 (
    ._1__1A(in_1[0]), ._2__1B(in_1[1]), ._3__1Y(out_2), ._7__GND(1'b0), ._14__Vcc(1'b1));  // open: _4__2A, _5__2B, _6__2Y, _13__4B, _12__4A, _11__4Y, _10__3B, _9__3A, _8__3Y
endmodule

// AND4
module AND1bit4X1 (
  input  [3:0] in_1,
  output out_2
);

  wire [1:0] and1bit2x1_1_out_2;

  AND1bit2X1 and1bit2x1_1 (.in_1(in_1[1:0]), .out_2(and1bit2x1_1_out_2[0]));
  AND1bit2X1 and1bit2x1_2 (.in_1(in_1[3:2]), .out_2(and1bit2x1_1_out_2[1]));
  AND1bit2X1 and1bit2x1_3 (.in_1(and1bit2x1_1_out_2), .out_2(out_2));
endmodule

// AND8
module AND1bit8X1 (
  input  [7:0] in_1,
  output out_2
);

  wire [1:0] and1bit4x1_1_out_2;

  AND1bit4X1 and1bit4x1_1 (.in_1(in_1[3:0]), .out_2(and1bit4x1_1_out_2[0]));
  AND1bit4X1 and1bit4x1_2 (.in_1(in_1[7:4]), .out_2(and1bit4x1_1_out_2[1]));
  AND1bit2X1 and1bit2x1_1 (.in_1(and1bit4x1_1_out_2), .out_2(out_2));
endmodule

// AND16
module AND1bit16X1 (
  input  [15:0] in_1,
  output out_2
);

  wire [1:0] and1bit8x1_1_out_2;

  AND1bit8X1 and1bit8x1_1 (.in_1(in_1[7:0]), .out_2(and1bit8x1_1_out_2[0]));
  AND1bit8X1 and1bit8x1_2 (.in_1(in_1[15:8]), .out_2(and1bit8x1_1_out_2[1]));
  AND1bit2X1 and1bit2x1_1 (.in_1(and1bit8x1_1_out_2), .out_2(out_2));
endmodule

// OR2
module OR1bit2X1 (
  input  [1:0] in_1,
  output out_2
);

  _7432 u_7432_1 (
    ._1__1A(in_1[0]), ._2__1B(in_1[1]), ._3__1Y(out_2), ._7__GND(1'b0), ._14__Vcc(1'b1));  // open: _4__2A, _5__2B, _6__2Y, _13__4B, _12__4A, _11__4Y, _10__3B, _9__3A, _8__3Y
endmodule

// OR3
module OR1BIT3X1 (
  input  [2:0] Input_A,
  output Output
);

  wire n7432_1__3__1y;

  _7432 u_7432_1 (
    ._1__1A(Input_A[0]), ._2__1B(Input_A[1]), ._3__1Y(n7432_1__3__1y), ._4__2A(n7432_1__3__1y),
    ._5__2B(Input_A[2]), ._6__2Y(Output), ._7__GND(1'b0), ._14__Vcc(1'b1));  // open: _13__4B, _12__4A, _11__4Y, _10__3B, _9__3A, _8__3Y
endmodule

// OR4
module OR1BIT4X1 (
  input  [3:0] Input_A,
  output Output
);

  wire n7432_1__3__1y, n7432_1__6__2y;

  _7432 u_7432_1 (
    ._1__1A(Input_A[0]), ._2__1B(Input_A[1]), ._3__1Y(n7432_1__3__1y), ._4__2A(n7432_1__3__1y),
    ._5__2B(Input_A[2]), ._6__2Y(n7432_1__6__2y), ._7__GND(1'b0), ._14__Vcc(1'b1), ._13__4B(n7432_1__6__2y),
    ._12__4A(Input_A[3]), ._11__4Y(Output));  // open: _10__3B, _9__3A, _8__3Y
endmodule

// OR8
module OR1BIT8X1 (
  input  [7:0] in_1,
  output out_2
);

  wire [1:0] or1bit4x1_2_output;

  OR1BIT4X1 or1bit4x1_1 (.Input_A(in_1[7:4]), .Output(or1bit4x1_2_output[1]));
  OR1BIT4X1 or1bit4x1_2 (.Input_A(in_1[3:0]), .Output(or1bit4x1_2_output[0]));
  OR1bit2X1 or1bit2x1_1 (.in_1(or1bit4x1_2_output), .out_2(out_2));
endmodule

// OR11
module OR1BIT11X1 (
  input  [10:0] in_1,
  output out_2
);

  wire [3:3] or1bit8x1_1_out_2;

  OR1BIT8X1 or1bit8x1_1 (.in_1(in_1[10:3]), .out_2(or1bit8x1_1_out_2[3]));
  OR1BIT4X1 or1bit4x1_1 (.Input_A({or1bit8x1_1_out_2[3], in_1[2:0]}), .Output(out_2));
endmodule

// OR16
module OR1BIT16X1 (
  input  [15:0] in_1,
  output out_2
);

  wire [1:0] or1bit8x1_1_out_2;

  OR1BIT8X1 or1bit8x1_1 (.in_1(in_1[7:0]), .out_2(or1bit8x1_1_out_2[0]));
  OR1BIT8X1 or1bit8x1_2 (.in_1(in_1[15:8]), .out_2(or1bit8x1_1_out_2[1]));
  OR1bit2X1 or1bit2x1_1 (.in_1(or1bit8x1_1_out_2), .out_2(out_2));
endmodule

// OR20
module OR1BIT20X1 (
  input  [19:0] in_1,
  output out_2
);

  wire [1:0] or1bit4x1_1_output;

  OR1BIT16X1 or1bit16x1_1 (.in_1(in_1[19:4]), .out_2(or1bit4x1_1_output[1]));
  OR1BIT4X1 or1bit4x1_1 (.Input_A(in_1[3:0]), .Output(or1bit4x1_1_output[0]));
  OR1bit2X1 or1bit2x1_1 (.in_1(or1bit4x1_1_output), .out_2(out_2));
endmodule

// A3
module Adder3bit (
  input  Cin,
  input  [2:0] Data0,
  input  [2:0] Data1,
  output [2:0] DataOut,
  output Cout
);

  _7483 u_7483_1 (
    ._1__A4(1'b0), ._2__S3(DataOut[2]), ._3__A3(Data0[2]), ._4__B3(Data1[2]), ._5__Vcc(1'b1),
    ._6__S2(DataOut[1]), ._7__B2(Data1[1]), ._8__A2(Data0[1]), ._16__B4(1'b0), ._15__S4(Cout),
    ._13__Cin(Cin), ._12__GND(1'b0), ._11__B1(Data1[0]), ._10__A1(Data0[0]), ._9__S1(DataOut[0]));  // open: _14__Cout
endmodule

// A4
module Adder4bit (
  input  Cin,
  input  [3:0] Data0,
  input  [3:0] Data1,
  output [3:0] DataOut,
  output Cout
);

  _7483 u_7483_1 (
    ._1__A4(Data0[3]), ._2__S3(DataOut[2]), ._3__A3(Data0[2]), ._4__B3(Data1[2]), ._5__Vcc(1'b1),
    ._6__S2(DataOut[1]), ._7__B2(Data1[1]), ._8__A2(Data0[1]), ._16__B4(Data1[3]), ._15__S4(DataOut[3]),
    ._14__Cout(Cout), ._13__Cin(Cin), ._12__GND(1'b0), ._11__B1(Data1[0]), ._10__A1(Data0[0]),
    ._9__S1(DataOut[0]));
endmodule

// A8
module Adder8bit (
  input  Cin,
  input  [7:0] Data0,
  input  [7:0] Data1,
  output [7:0] DataOut,
  output Cout
);

  wire adder4bit_1_cout;

  Adder4bit adder4bit_1 (
    .Data0(Data0[3:0]), .Data1(Data1[3:0]), .Cin(Cin), .Cout(adder4bit_1_cout), .DataOut(DataOut[3:0]));
  Adder4bit adder4bit_2 (
    .Data0(Data0[7:4]), .Data1(Data1[7:4]), .Cin(adder4bit_1_cout), .Cout(Cout), .DataOut(DataOut[7:4]));
endmodule

// A11
module Adder11bit (
  input  Cin,
  input  [10:0] Data0,
  input  [10:0] Data1,
  output [10:0] DataOut,
  output Cout
);

  wire adder4bit_1_cout, adder4bit_2_cout;

  Adder4bit adder4bit_1 (
    .Data0(Data0[3:0]), .Data1(Data1[3:0]), .Cin(Cin), .Cout(adder4bit_1_cout), .DataOut(DataOut[3:0]));
  Adder4bit adder4bit_2 (
    .Data0(Data0[7:4]), .Data1(Data1[7:4]), .Cin(adder4bit_1_cout), .Cout(adder4bit_2_cout),
    .DataOut(DataOut[7:4]));
  Adder3bit adder3bit_1 (
    .Data0(Data0[10:8]), .Data1(Data1[10:8]), .Cin(adder4bit_2_cout), .Cout(Cout), .DataOut(DataOut[10:8]));
endmodule

// A20
module Adder20bit (
  input  Cin,
  input  [19:0] Data0,
  input  [19:0] Data1,
  output Cout,
  output [19:0] DataOut
);

  wire adder4bit_1_cout, adder4bit_2_cout, adder4bit_3_cout, adder4bit_4_cout;

  Adder4bit adder4bit_1 (
    .Data0(Data0[3:0]), .Data1(Data1[3:0]), .Cin(Cin), .Cout(adder4bit_1_cout), .DataOut(DataOut[3:0]));
  Adder4bit adder4bit_2 (
    .Data0(Data0[7:4]), .Data1(Data1[7:4]), .Cin(adder4bit_1_cout), .Cout(adder4bit_2_cout),
    .DataOut(DataOut[7:4]));
  Adder4bit adder4bit_3 (
    .Data0(Data0[11:8]), .Data1(Data1[11:8]), .Cin(adder4bit_2_cout), .Cout(adder4bit_3_cout),
    .DataOut(DataOut[11:8]));
  Adder4bit adder4bit_4 (
    .Data0(Data0[15:12]), .Data1(Data1[15:12]), .Cin(adder4bit_3_cout), .Cout(adder4bit_4_cout),
    .DataOut(DataOut[15:12]));
  Adder4bit adder4bit_5 (
    .Data0(Data0[19:16]), .Data1(Data1[19:16]), .Cin(adder4bit_4_cout), .Cout(Cout), .DataOut(DataOut[19:16]));
endmodule

// A23
module Adder23bit (
  input  Cin,
  input  [22:0] Data0,
  input  [22:0] Data1,
  output Cout,
  output [22:0] DataOut
);

  wire adder4bit_1_cout, adder4bit_2_cout, adder4bit_3_cout, adder4bit_4_cout, adder4bit_5_cout;

  Adder4bit adder4bit_1 (
    .Data0(Data0[3:0]), .Data1(Data1[3:0]), .Cin(Cin), .Cout(adder4bit_1_cout), .DataOut(DataOut[3:0]));
  Adder4bit adder4bit_2 (
    .Data0(Data0[7:4]), .Data1(Data1[7:4]), .Cin(adder4bit_1_cout), .Cout(adder4bit_2_cout),
    .DataOut(DataOut[7:4]));
  Adder4bit adder4bit_3 (
    .Data0(Data0[11:8]), .Data1(Data1[11:8]), .Cin(adder4bit_2_cout), .Cout(adder4bit_3_cout),
    .DataOut(DataOut[11:8]));
  Adder4bit adder4bit_4 (
    .Data0(Data0[15:12]), .Data1(Data1[15:12]), .Cin(adder4bit_3_cout), .Cout(adder4bit_4_cout),
    .DataOut(DataOut[15:12]));
  Adder4bit adder4bit_5 (
    .Data0(Data0[19:16]), .Data1(Data1[19:16]), .Cin(adder4bit_4_cout), .Cout(adder4bit_5_cout),
    .DataOut(DataOut[19:16]));
  Adder3bit adder3bit_1 (
    .Data0(Data0[22:20]), .Data1(Data1[22:20]), .Cin(adder4bit_5_cout), .Cout(Cout), .DataOut(DataOut[22:20]));
endmodule

// A26
module Adder26bit (
  input  Cin,
  input  [25:0] Data0,
  input  [25:0] Data1,
  output Cout,
  output [25:0] DataOut
);

  wire adder3bit_1_cout, adder4bit_1_cout, adder4bit_2_cout, adder4bit_3_cout, adder4bit_4_cout,
       adder4bit_5_cout;

  Adder4bit adder4bit_1 (
    .Data0(Data0[3:0]), .Data1(Data1[3:0]), .Cin(Cin), .Cout(adder4bit_1_cout), .DataOut(DataOut[3:0]));
  Adder4bit adder4bit_2 (
    .Data0(Data0[7:4]), .Data1(Data1[7:4]), .Cin(adder4bit_1_cout), .Cout(adder4bit_2_cout),
    .DataOut(DataOut[7:4]));
  Adder4bit adder4bit_3 (
    .Data0(Data0[11:8]), .Data1(Data1[11:8]), .Cin(adder4bit_2_cout), .Cout(adder4bit_3_cout),
    .DataOut(DataOut[11:8]));
  Adder4bit adder4bit_4 (
    .Data0(Data0[15:12]), .Data1(Data1[15:12]), .Cin(adder4bit_3_cout), .Cout(adder4bit_4_cout),
    .DataOut(DataOut[15:12]));
  Adder4bit adder4bit_5 (
    .Data0(Data0[19:16]), .Data1(Data1[19:16]), .Cin(adder4bit_4_cout), .Cout(adder4bit_5_cout),
    .DataOut(DataOut[19:16]));
  Adder3bit adder3bit_1 (
    .Data0(Data0[22:20]), .Data1(Data1[22:20]), .Cin(adder4bit_5_cout), .Cout(adder3bit_1_cout),
    .DataOut(DataOut[22:20]));
  Adder3bit adder3bit_2 (
    .Data0(Data0[25:23]), .Data1(Data1[25:23]), .Cin(adder3bit_1_cout), .Cout(Cout), .DataOut(DataOut[25:23]));
endmodule

// A29
module Adder29bit (
  input  Cin,
  input  [28:0] Data0,
  input  [28:0] Data1,
  output [28:0] DataOut,
  output Cout
);

  wire adder3bit_1_cout, adder3bit_2_cout, adder4bit_1_cout, adder4bit_2_cout, adder4bit_3_cout,
       adder4bit_4_cout, adder4bit_5_cout;

  Adder4bit adder4bit_1 (
    .Data0(Data0[3:0]), .Data1(Data1[3:0]), .Cin(Cin), .Cout(adder4bit_1_cout), .DataOut(DataOut[3:0]));
  Adder4bit adder4bit_2 (
    .Data0(Data0[7:4]), .Data1(Data1[7:4]), .Cin(adder4bit_1_cout), .Cout(adder4bit_2_cout),
    .DataOut(DataOut[7:4]));
  Adder4bit adder4bit_3 (
    .Data0(Data0[11:8]), .Data1(Data1[11:8]), .Cin(adder4bit_2_cout), .Cout(adder4bit_3_cout),
    .DataOut(DataOut[11:8]));
  Adder4bit adder4bit_4 (
    .Data0(Data0[15:12]), .Data1(Data1[15:12]), .Cin(adder4bit_3_cout), .Cout(adder4bit_4_cout),
    .DataOut(DataOut[15:12]));
  Adder4bit adder4bit_5 (
    .Data0(Data0[19:16]), .Data1(Data1[19:16]), .Cin(adder4bit_4_cout), .Cout(adder4bit_5_cout),
    .DataOut(DataOut[19:16]));
  Adder3bit adder3bit_1 (
    .Data0(Data0[22:20]), .Data1(Data1[22:20]), .Cin(adder4bit_5_cout), .Cout(adder3bit_1_cout),
    .DataOut(DataOut[22:20]));
  Adder3bit adder3bit_2 (
    .Data0(Data0[25:23]), .Data1(Data1[25:23]), .Cin(adder3bit_1_cout), .Cout(adder3bit_2_cout),
    .DataOut(DataOut[25:23]));
  Adder3bit adder3bit_3 (
    .Data0(Data0[28:26]), .Data1(Data1[28:26]), .Cin(adder3bit_2_cout), .Cout(Cout), .DataOut(DataOut[28:26]));
endmodule

// A32
module Adder32bit (
  input  Cin,
  input  [31:0] Data0,
  input  [31:0] Data1,
  output [31:0] DataOut,
  output Cout
);

  wire adder4bit_1_cout, adder4bit_2_cout, adder4bit_3_cout, adder4bit_4_cout, adder4bit_5_cout,
       adder4bit_6_cout, adder4bit_7_cout;

  Adder4bit adder4bit_1 (
    .Data0(Data0[3:0]), .Data1(Data1[3:0]), .Cin(Cin), .Cout(adder4bit_1_cout), .DataOut(DataOut[3:0]));
  Adder4bit adder4bit_2 (
    .Data0(Data0[7:4]), .Data1(Data1[7:4]), .Cin(adder4bit_1_cout), .Cout(adder4bit_2_cout),
    .DataOut(DataOut[7:4]));
  Adder4bit adder4bit_3 (
    .Data0(Data0[11:8]), .Data1(Data1[11:8]), .Cin(adder4bit_2_cout), .Cout(adder4bit_3_cout),
    .DataOut(DataOut[11:8]));
  Adder4bit adder4bit_4 (
    .Data0(Data0[15:12]), .Data1(Data1[15:12]), .Cin(adder4bit_3_cout), .Cout(adder4bit_4_cout),
    .DataOut(DataOut[15:12]));
  Adder4bit adder4bit_5 (
    .Data0(Data0[19:16]), .Data1(Data1[19:16]), .Cin(adder4bit_4_cout), .Cout(adder4bit_5_cout),
    .DataOut(DataOut[19:16]));
  Adder4bit adder4bit_6 (
    .Data0(Data0[23:20]), .Data1(Data1[23:20]), .Cin(adder4bit_5_cout), .Cout(adder4bit_6_cout),
    .DataOut(DataOut[23:20]));
  Adder4bit adder4bit_7 (
    .Data0(Data0[27:24]), .Data1(Data1[27:24]), .Cin(adder4bit_6_cout), .Cout(adder4bit_7_cout),
    .DataOut(DataOut[27:24]));
  Adder4bit adder4bit_8 (
    .Data0(Data0[31:28]), .Data1(Data1[31:28]), .Cin(adder4bit_7_cout), .Cout(Cout), .DataOut(DataOut[31:28]));
endmodule

// XOR1
module XOR1bit2X1 (
  input  Input_A,
  input  Input_B,
  output Output
);

  _7486 u_7486_1 (
    ._1__1A(Input_A), ._2__1B(Input_B), ._3__1Y(Output), ._7__GND(1'b0), ._14__Vcc(1'b1));  // open: _4__2A, _5__2B, _6__2Y, _13__4B, _12__4A, _11__4Y, _10__3B, _9__3A, _8__3Y
endmodule

// XOR3
module XOR3bit2X1 (
  input  [2:0] Input_A,
  input  [2:0] Input_B,
  output [2:0] Output
);

  _7486 u_7486_1 (
    ._1__1A(Input_A[0]), ._2__1B(Input_B[0]), ._3__1Y(Output[0]), ._4__2A(Input_A[1]), ._5__2B(Input_B[1]),
    ._6__2Y(Output[1]), ._7__GND(1'b0), ._14__Vcc(1'b1), ._13__4B(Input_A[2]), ._12__4A(Input_B[2]),
    ._11__4Y(Output[2]));  // open: _10__3B, _9__3A, _8__3Y
endmodule

// XOR4
module XOR4bit2X1 (
  input  [3:0] Input_A,
  input  [3:0] Input_B,
  output [3:0] Output
);

  _7486 u_7486_1 (
    ._1__1A(Input_A[0]), ._2__1B(Input_B[0]), ._3__1Y(Output[0]), ._4__2A(Input_A[1]), ._5__2B(Input_B[1]),
    ._6__2Y(Output[1]), ._7__GND(1'b0), ._14__Vcc(1'b1), ._13__4B(Input_A[3]), ._12__4A(Input_B[3]),
    ._11__4Y(Output[3]), ._10__3B(Input_A[2]), ._9__3A(Input_B[2]), ._8__3Y(Output[2]));
endmodule

// XOR11
module XOR11bit2X1 (
  input  [10:0] Input_A,
  input  [10:0] Input_B,
  output [10:0] Output
);

  XOR4bit2X1 xor4bit2x1_1 (.Input_A(Input_A[3:0]), .Input_B(Input_B[3:0]), .Output(Output[3:0]));
  XOR4bit2X1 xor4bit2x1_2 (.Input_A(Input_A[7:4]), .Input_B(Input_B[7:4]), .Output(Output[7:4]));
  XOR3bit2X1 xor3bit2x1_1 (.Input_A(Input_A[10:8]), .Input_B(Input_B[10:8]), .Output(Output[10:8]));
endmodule

// XOR20
module XOR20bit2X1 (
  input  [19:0] Input_A,
  input  [19:0] Input_B,
  output [19:0] Output
);

  XOR4bit2X1 xor4bit2x1_1 (.Input_A(Input_A[3:0]), .Input_B(Input_B[3:0]), .Output(Output[3:0]));
  XOR4bit2X1 xor4bit2x1_2 (.Input_A(Input_A[7:4]), .Input_B(Input_B[7:4]), .Output(Output[7:4]));
  XOR4bit2X1 xor4bit2x1_3 (.Input_A(Input_A[11:8]), .Input_B(Input_B[11:8]), .Output(Output[11:8]));
  XOR4bit2X1 xor4bit2x1_4 (.Input_A(Input_A[15:12]), .Input_B(Input_B[15:12]), .Output(Output[15:12]));
  XOR4bit2X1 xor4bit2x1_5 (.Input_A(Input_A[19:16]), .Input_B(Input_B[19:16]), .Output(Output[19:16]));
endmodule

// XOR32
module XOR32bit2X1 (
  input  [31:0] Input_A,
  input  [31:0] Input_B,
  output [31:0] Output
);

  XOR4bit2X1 xor4bit2x1_1 (.Input_A(Input_A[3:0]), .Input_B(Input_B[3:0]), .Output(Output[3:0]));
  XOR4bit2X1 xor4bit2x1_2 (.Input_A(Input_A[7:4]), .Input_B(Input_B[7:4]), .Output(Output[7:4]));
  XOR4bit2X1 xor4bit2x1_3 (.Input_A(Input_A[11:8]), .Input_B(Input_B[11:8]), .Output(Output[11:8]));
  XOR4bit2X1 xor4bit2x1_4 (.Input_A(Input_A[15:12]), .Input_B(Input_B[15:12]), .Output(Output[15:12]));
  XOR4bit2X1 xor4bit2x1_5 (.Input_A(Input_A[19:16]), .Input_B(Input_B[19:16]), .Output(Output[19:16]));
  XOR4bit2X1 xor4bit2x1_6 (.Input_A(Input_A[23:20]), .Input_B(Input_B[23:20]), .Output(Output[23:20]));
  XOR4bit2X1 xor4bit2x1_7 (.Input_A(Input_A[27:24]), .Input_B(Input_B[27:24]), .Output(Output[27:24]));
  XOR4bit2X1 xor4bit2x1_8 (.Input_A(Input_A[31:28]), .Input_B(Input_B[31:28]), .Output(Output[31:28]));
endmodule

// NOT1
module NOT1bit (
  input  Input,
  output Output
);

  _7404 u_7404_1 (
    ._1__1A(Input), ._2__1Y(Output), ._7__GND(1'b0), ._14__Vcc(1'b1));  // open: _3__2A, _4__2Y, _5__3A, _6__3Y, _13__6A, _12__6Y, _11__5A, _10__5Y, _9__4A, _8__4Y
endmodule

// NOT3
module NOT3bit (
  input  [2:0] Input,
  output [2:0] Output
);

  _7404 u_7404_1 (
    ._1__1A(Input[0]), ._2__1Y(Output[0]), ._3__2A(Input[1]), ._4__2Y(Output[1]), ._5__3A(Input[2]),
    ._6__3Y(Output[2]), ._7__GND(1'b0), ._14__Vcc(1'b1));  // open: _13__6A, _12__6Y, _11__5A, _10__5Y, _9__4A, _8__4Y
endmodule

// NOT4
module NOT4bit (
  input  [3:0] Input,
  output [3:0] Output
);

  _7404 u_7404_1 (
    ._1__1A(Input[0]), ._2__1Y(Output[0]), ._3__2A(Input[1]), ._4__2Y(Output[1]), ._5__3A(Input[2]),
    ._6__3Y(Output[2]), ._7__GND(1'b0), ._14__Vcc(1'b1), ._13__6A(Input[3]), ._12__6Y(Output[3]));  // open: _11__5A, _10__5Y, _9__4A, _8__4Y
endmodule

// NOT11
module NOT11bit (
  input  [10:0] Input,
  output [10:0] Output
);

  NOT4bit not4bit_1 (.Input(Input[3:0]), .Output(Output[3:0]));
  NOT4bit not4bit_2 (.Input(Input[7:4]), .Output(Output[7:4]));
  NOT3bit not3bit_1 (.Input(Input[10:8]), .Output(Output[10:8]));
endmodule

// NOT20
module NOT20bit (
  input  [19:0] Input,
  output [19:0] Output
);

  NOT4bit not4bit_1 (.Input(Input[3:0]), .Output(Output[3:0]));
  NOT4bit not4bit_2 (.Input(Input[7:4]), .Output(Output[7:4]));
  NOT4bit not4bit_3 (.Input(Input[11:8]), .Output(Output[11:8]));
  NOT4bit not4bit_4 (.Input(Input[15:12]), .Output(Output[15:12]));
  NOT4bit not4bit_5 (.Input(Input[19:16]), .Output(Output[19:16]));
endmodule

// Zero
module ZERO32bit (
  output [31:0] out_1
);


  assign out_1 = {32{1'b0}};
endmodule

// IS
module InputSplitter (
  input  [31:0] _32,
  output s1,
  output [10:0] e11,
  output [19:0] f20
);


  assign e11 = _32[30:20];
  assign f20 = _32[19:0];
  assign s1 = _32[31];
endmodule

// OS
module OutputSplitter (
  input  _1,
  input  [10:0] _11,
  input  [19:0] _20,
  output [31:0] _32
);


  assign _32 = {_1, _11, _20};
endmodule

// >>
module CustomRightShifter (
  input  Shift_bit,
  input  [31:0] Data_in,
  input  [10:0] Shift_amount,
  output [31:0] Data_out
);

  wire or1bit4x1_1_output;
  wire [0:0] mux32bit2x1_5_dataout, or1bit3x1_1_output;
  wire [1:0] mux32bit2x1_4_dataout;
  wire [3:0] mux32bit2x1_3_dataout;
  wire [7:0] mux32bit2x1_2_dataout;
  wire [15:0] mux32bit2x1_1_dataout, mux32bit2x1_1_dataout_2;
  wire [23:0] mux32bit2x1_2_dataout_2;
  wire [27:0] mux32bit2x1_3_dataout_2;
  wire [29:0] mux32bit2x1_4_dataout_2;
  wire [30:0] mux32bit2x1_5_dataout_2;

  OR1BIT3X1 or1bit3x1_1 (
    .Input_A({Shift_amount[8], Shift_amount[9], Shift_amount[10]}), .Output(or1bit3x1_1_output[0]));
  OR1BIT4X1 or1bit4x1_1 (
    .Input_A({Shift_amount[5], Shift_amount[6], Shift_amount[7], or1bit3x1_1_output[0]}),
    .Output(or1bit4x1_1_output));
  MUX32bit2x1 mux32bit2x1_1 (
    .S(or1bit4x1_1_output), .Data0(Data_in), .Data1({32{1'b0}}),
    .DataOut({mux32bit2x1_1_dataout_2, mux32bit2x1_1_dataout}));
  MUX32bit2x1 mux32bit2x1_2 (
    .S(Shift_amount[4]), .Data0({mux32bit2x1_1_dataout_2, mux32bit2x1_1_dataout}),
    .Data1({{16{Shift_bit}}, mux32bit2x1_1_dataout_2}),
    .DataOut({mux32bit2x1_2_dataout_2, mux32bit2x1_2_dataout}));
  MUX32bit2x1 mux32bit2x1_3 (
    .S(Shift_amount[3]), .Data0({mux32bit2x1_2_dataout_2, mux32bit2x1_2_dataout}),
    .Data1({{8{Shift_bit}}, mux32bit2x1_2_dataout_2}),
    .DataOut({mux32bit2x1_3_dataout_2, mux32bit2x1_3_dataout}));
  MUX32bit2x1 mux32bit2x1_4 (
    .S(Shift_amount[2]), .Data0({mux32bit2x1_3_dataout_2, mux32bit2x1_3_dataout}),
    .Data1({{4{Shift_bit}}, mux32bit2x1_3_dataout_2}),
    .DataOut({mux32bit2x1_4_dataout_2, mux32bit2x1_4_dataout}));
  MUX32bit2x1 mux32bit2x1_5 (
    .S(Shift_amount[1]), .Data0({mux32bit2x1_4_dataout_2, mux32bit2x1_4_dataout}),
    .Data1({{2{Shift_bit}}, mux32bit2x1_4_dataout_2}),
    .DataOut({mux32bit2x1_5_dataout_2, mux32bit2x1_5_dataout[0]}));
  MUX32bit2x1 mux32bit2x1_6 (
    .S(Shift_amount[0]), .Data0({mux32bit2x1_5_dataout_2, mux32bit2x1_5_dataout[0]}),
    .Data1({Shift_bit, mux32bit2x1_5_dataout_2}), .DataOut(Data_out));
endmodule

// <<
module CustomLeftShifter (
  input  Shift_bit,
  input  [31:0] Data_in,
  input  [10:0] Shift_amount,
  output [31:0] Data_out
);

  wire or1bit4x1_1_output;
  wire [0:0] or1bit3x1_1_output;
  wire [31:0] mux32bit2x1_4_dataout;
  wire [31:1] mux32bit2x1_5_dataout;
  wire [31:4] mux32bit2x1_3_dataout;
  wire [31:8] mux32bit2x1_2_dataout;
  wire [31:16] mux32bit2x1_1_dataout, mux32bit2x1_1_dataout_2;
  wire [31:24] mux32bit2x1_2_dataout_2;
  wire [31:28] mux32bit2x1_3_dataout_2;
  wire [31:31] mux32bit2x1_5_dataout_2;

  OR1BIT3X1 or1bit3x1_1 (
    .Input_A({Shift_amount[8], Shift_amount[9], Shift_amount[10]}), .Output(or1bit3x1_1_output[0]));
  OR1BIT4X1 or1bit4x1_1 (
    .Input_A({Shift_amount[5], Shift_amount[6], Shift_amount[7], or1bit3x1_1_output[0]}),
    .Output(or1bit4x1_1_output));
  MUX32bit2x1 mux32bit2x1_1 (
    .S(or1bit4x1_1_output), .Data0(Data_in), .Data1({32{1'b0}}),
    .DataOut({mux32bit2x1_1_dataout_2, mux32bit2x1_1_dataout}));
  MUX32bit2x1 mux32bit2x1_2 (
    .S(Shift_amount[4]), .Data0({mux32bit2x1_1_dataout_2, mux32bit2x1_1_dataout}),
    .Data1({mux32bit2x1_1_dataout, {16{Shift_bit}}}),
    .DataOut({mux32bit2x1_2_dataout_2, mux32bit2x1_2_dataout}));
  MUX32bit2x1 mux32bit2x1_3 (
    .S(Shift_amount[3]), .Data0({mux32bit2x1_2_dataout_2, mux32bit2x1_2_dataout}),
    .Data1({mux32bit2x1_2_dataout, {8{Shift_bit}}}),
    .DataOut({mux32bit2x1_3_dataout_2, mux32bit2x1_3_dataout}));
  MUX32bit2x1 mux32bit2x1_4 (
    .S(Shift_amount[2]), .Data0({mux32bit2x1_3_dataout_2, mux32bit2x1_3_dataout}),
    .Data1({mux32bit2x1_3_dataout, {4{Shift_bit}}}), .DataOut(mux32bit2x1_4_dataout));
  MUX32bit2x1 mux32bit2x1_5 (
    .S(Shift_amount[1]), .Data0(mux32bit2x1_4_dataout),
    .Data1({mux32bit2x1_4_dataout[29:0], {2{Shift_bit}}}),
    .DataOut({mux32bit2x1_5_dataout_2[31], mux32bit2x1_5_dataout}));
  MUX32bit2x1 mux32bit2x1_6 (
    .S(Shift_amount[0]), .Data0({mux32bit2x1_5_dataout_2[31], mux32bit2x1_5_dataout}),
    .Data1({mux32bit2x1_5_dataout, Shift_bit}), .DataOut(Data_out));
endmodule

// MS
module makeSignificand (
  input  [19:0] in20,
  output [31:0] out32
);


  assign out32 = {1'b1, in20, {11{1'b0}}};
endmodule

// Comp4
module CompareWith4 (
  input  [2:0] in_1,
  output out_2,
  output out_3,
  output out_4
);

  wire [0:0] not1bit_1_output, not1bit_2_output;
  wire [1:0] adder3bit_2_cout;
  wire [2:0] not3bit_1_output, not3bit_2_output;

  NOT3bit not3bit_1 (.Input(3'b100), .Output(not3bit_1_output));
  NOT3bit not3bit_2 (.Input(in_1), .Output(not3bit_2_output));
  Adder3bit adder3bit_1 (
    .Data0(in_1), .Data1(not3bit_1_output), .Cin(1'b1), .Cout(adder3bit_2_cout[0]));  // open: DataOut
  Adder3bit adder3bit_2 (
    .Data0(3'b100), .Data1(not3bit_2_output), .Cin(1'b1), .Cout(adder3bit_2_cout[1]));  // open: DataOut
  NOT1bit not1bit_1 (.Input(adder3bit_2_cout[0]), .Output(not1bit_1_output[0]));
  NOT1bit not1bit_2 (.Input(adder3bit_2_cout[1]), .Output(not1bit_2_output[0]));
  AND1bit2X1 and1bit2x1_1 (.in_1({adder3bit_2_cout[1], not1bit_1_output[0]}), .out_2(out_2));
  AND1bit2X1 and1bit2x1_2 (.in_1(adder3bit_2_cout), .out_2(out_3));
  AND1bit2X1 and1bit2x1_3 (.in_1({adder3bit_2_cout[0], not1bit_2_output[0]}), .out_2(out_4));
endmodule

// GRS
module StickyAdderBit (
  input  [3:0] LGRS,
  output addBit
);

  wire [0:0] comparewith4_1_out_2, comparewith4_1_out_3, comparewith4_1_out_4;
  wire [1:0] and1bit2x1_1_out_2, or1bit2x1_1_out_2;

  CompareWith4 comparewith4_1 (
    .in_1(LGRS[2:0]), .out_2(comparewith4_1_out_2[0]), .out_3(comparewith4_1_out_3[0]),
    .out_4(comparewith4_1_out_4[0]));
  AND1bit2X1 and1bit2x1_1 (.in_1({1'b0, comparewith4_1_out_2[0]}), .out_2(and1bit2x1_1_out_2[0]));
  OR1bit2X1 or1bit2x1_1 (.in_1(and1bit2x1_1_out_2), .out_2(or1bit2x1_1_out_2[0]));
  AND1bit2X1 and1bit2x1_2 (.in_1({LGRS[3], comparewith4_1_out_3[0]}), .out_2(and1bit2x1_1_out_2[1]));
  AND1bit2X1 and1bit2x1_3 (.in_1({1'b1, comparewith4_1_out_4[0]}), .out_2(or1bit2x1_1_out_2[1]));
  OR1bit2X1 or1bit2x1_2 (.in_1(or1bit2x1_1_out_2), .out_2(addBit));
endmodule

// IncExp
module IncrementExponent (
  input  [10:0] A,
  output [10:0] A_1,
  output Overflow
);

  Adder11bit adder11bit_1 (.Data0({11{1'b0}}), .Data1(A), .Cin(1'b1), .Cout(Overflow), .DataOut(A_1));
endmodule

// InvSel
module SelectInverse (
  input  [31:0] Data_in,
  input  Selector,
  output [31:0] DataOut
);

  XOR32bit2X1 xor32bit2x1_1 (.Input_A(Data_in), .Input_B({32{Selector}}), .Output(DataOut));
endmodule

// Prio
module PriorityEncoder (
  input  [31:0] in_1,
  output [10:0] out_2
);

  wire and1bit2x1_61_out_2;
  wire [0:0] not1bit_22_output;
  wire [1:0] not1bit_1_output, not1bit_3_output, not1bit_4_output, not1bit_5_output, not1bit_6_output,
       not1bit_7_output, not1bit_8_output, not1bit_9_output, not1bit_10_output, not1bit_11_output,
       not1bit_12_output, not1bit_13_output, not1bit_14_output, not1bit_15_output, not1bit_16_output,
       not1bit_17_output, not1bit_18_output, not1bit_19_output, not1bit_20_output, not1bit_21_output,
       not1bit_23_output, not1bit_24_output, not1bit_25_output, not1bit_26_output, not1bit_27_output,
       not1bit_28_output, not1bit_29_output, not1bit_30_output, not1bit_31_output, not1bit_32_output;
  wire [1:1] and1bit2x1_39_out_2;
  wire [11:3] and1bit2x1_16_out_2;
  wire [15:0] and1bit2x1_6_out_2;
  wire [15:2] and1bit2x1_2_out_2;
  wire [15:7] and1bit2x1_14_out_2;
  wire [15:15] and1bit2x1_30_out_2;

  NOT1bit not1bit_1 (.Input(in_1[30]), .Output(not1bit_1_output[0]));
  NOT1bit not1bit_2 (.Input(in_1[31]), .Output(not1bit_1_output[1]));
  AND1bit2X1 and1bit2x1_1 (.in_1(not1bit_1_output), .out_2(not1bit_3_output[1]));
  AND1bit2X1 and1bit2x1_2 (.in_1({not1bit_1_output[1], in_1[30]}), .out_2(and1bit2x1_2_out_2[15]));
  NOT1bit not1bit_3 (.Input(in_1[29]), .Output(not1bit_3_output[0]));
  AND1bit2X1 and1bit2x1_3 (.in_1(not1bit_3_output), .out_2(not1bit_4_output[1]));
  AND1bit2X1 and1bit2x1_4 (.in_1({not1bit_3_output[1], in_1[29]}), .out_2(and1bit2x1_2_out_2[14]));
  NOT1bit not1bit_4 (.Input(in_1[28]), .Output(not1bit_4_output[0]));
  AND1bit2X1 and1bit2x1_5 (.in_1(not1bit_4_output), .out_2(not1bit_5_output[1]));
  AND1bit2X1 and1bit2x1_6 (.in_1({not1bit_4_output[1], in_1[28]}), .out_2(and1bit2x1_6_out_2[15]));
  NOT1bit not1bit_5 (.Input(in_1[27]), .Output(not1bit_5_output[0]));
  AND1bit2X1 and1bit2x1_7 (.in_1(not1bit_5_output), .out_2(not1bit_6_output[1]));
  AND1bit2X1 and1bit2x1_8 (.in_1({not1bit_5_output[1], in_1[27]}), .out_2(and1bit2x1_6_out_2[14]));
  NOT1bit not1bit_6 (.Input(in_1[26]), .Output(not1bit_6_output[0]));
  AND1bit2X1 and1bit2x1_9 (.in_1(not1bit_6_output), .out_2(not1bit_7_output[1]));
  AND1bit2X1 and1bit2x1_10 (.in_1({not1bit_6_output[1], in_1[26]}), .out_2(and1bit2x1_6_out_2[13]));
  NOT1bit not1bit_7 (.Input(in_1[25]), .Output(not1bit_7_output[0]));
  AND1bit2X1 and1bit2x1_11 (.in_1(not1bit_7_output), .out_2(not1bit_8_output[1]));
  AND1bit2X1 and1bit2x1_12 (.in_1({not1bit_7_output[1], in_1[25]}), .out_2(and1bit2x1_6_out_2[12]));
  NOT1bit not1bit_8 (.Input(in_1[24]), .Output(not1bit_8_output[0]));
  AND1bit2X1 and1bit2x1_13 (.in_1(not1bit_8_output), .out_2(not1bit_9_output[1]));
  AND1bit2X1 and1bit2x1_14 (.in_1({not1bit_8_output[1], in_1[24]}), .out_2(and1bit2x1_14_out_2[15]));
  NOT1bit not1bit_9 (.Input(in_1[23]), .Output(not1bit_9_output[0]));
  AND1bit2X1 and1bit2x1_15 (.in_1(not1bit_9_output), .out_2(not1bit_10_output[1]));
  AND1bit2X1 and1bit2x1_16 (.in_1({not1bit_9_output[1], in_1[23]}), .out_2(and1bit2x1_16_out_2[11]));
  NOT1bit not1bit_10 (.Input(in_1[22]), .Output(not1bit_10_output[0]));
  AND1bit2X1 and1bit2x1_17 (.in_1(not1bit_10_output), .out_2(not1bit_11_output[1]));
  AND1bit2X1 and1bit2x1_18 (.in_1({not1bit_10_output[1], in_1[22]}), .out_2(and1bit2x1_2_out_2[11]));
  NOT1bit not1bit_11 (.Input(in_1[21]), .Output(not1bit_11_output[0]));
  AND1bit2X1 and1bit2x1_19 (.in_1(not1bit_11_output), .out_2(not1bit_12_output[1]));
  AND1bit2X1 and1bit2x1_20 (.in_1({not1bit_11_output[1], in_1[21]}), .out_2(and1bit2x1_2_out_2[10]));
  NOT1bit not1bit_12 (.Input(in_1[20]), .Output(not1bit_12_output[0]));
  AND1bit2X1 and1bit2x1_21 (.in_1(not1bit_12_output), .out_2(not1bit_13_output[1]));
  AND1bit2X1 and1bit2x1_22 (.in_1({not1bit_12_output[1], in_1[20]}), .out_2(and1bit2x1_6_out_2[11]));
  NOT1bit not1bit_13 (.Input(in_1[19]), .Output(not1bit_13_output[0]));
  AND1bit2X1 and1bit2x1_23 (.in_1(not1bit_13_output), .out_2(not1bit_14_output[1]));
  AND1bit2X1 and1bit2x1_24 (.in_1({not1bit_13_output[1], in_1[19]}), .out_2(and1bit2x1_6_out_2[10]));
  NOT1bit not1bit_14 (.Input(in_1[18]), .Output(not1bit_14_output[0]));
  AND1bit2X1 and1bit2x1_25 (.in_1(not1bit_14_output), .out_2(not1bit_15_output[1]));
  AND1bit2X1 and1bit2x1_26 (.in_1({not1bit_14_output[1], in_1[18]}), .out_2(and1bit2x1_6_out_2[9]));
  NOT1bit not1bit_15 (.Input(in_1[17]), .Output(not1bit_15_output[0]));
  AND1bit2X1 and1bit2x1_27 (.in_1(not1bit_15_output), .out_2(not1bit_16_output[1]));
  AND1bit2X1 and1bit2x1_28 (.in_1({not1bit_15_output[1], in_1[17]}), .out_2(and1bit2x1_6_out_2[8]));
  NOT1bit not1bit_16 (.Input(in_1[16]), .Output(not1bit_16_output[0]));
  AND1bit2X1 and1bit2x1_29 (.in_1(not1bit_16_output), .out_2(not1bit_17_output[1]));
  AND1bit2X1 and1bit2x1_30 (.in_1({not1bit_16_output[1], in_1[16]}), .out_2(and1bit2x1_30_out_2[15]));
  NOT1bit not1bit_17 (.Input(in_1[15]), .Output(not1bit_17_output[0]));
  AND1bit2X1 and1bit2x1_31 (.in_1(not1bit_17_output), .out_2(not1bit_18_output[1]));
  AND1bit2X1 and1bit2x1_32 (.in_1({not1bit_17_output[1], in_1[15]}), .out_2(and1bit2x1_16_out_2[7]));
  NOT1bit not1bit_18 (.Input(in_1[14]), .Output(not1bit_18_output[0]));
  AND1bit2X1 and1bit2x1_33 (.in_1(not1bit_18_output), .out_2(not1bit_19_output[1]));
  AND1bit2X1 and1bit2x1_34 (.in_1({not1bit_18_output[1], in_1[14]}), .out_2(and1bit2x1_2_out_2[7]));
  NOT1bit not1bit_19 (.Input(in_1[13]), .Output(not1bit_19_output[0]));
  AND1bit2X1 and1bit2x1_35 (.in_1(not1bit_19_output), .out_2(not1bit_20_output[1]));
  AND1bit2X1 and1bit2x1_36 (.in_1({not1bit_19_output[1], in_1[13]}), .out_2(and1bit2x1_2_out_2[6]));
  NOT1bit not1bit_20 (.Input(in_1[12]), .Output(not1bit_20_output[0]));
  AND1bit2X1 and1bit2x1_37 (.in_1(not1bit_20_output), .out_2(not1bit_21_output[1]));
  AND1bit2X1 and1bit2x1_38 (.in_1({not1bit_20_output[1], in_1[12]}), .out_2(and1bit2x1_6_out_2[7]));
  NOT1bit not1bit_21 (.Input(in_1[11]), .Output(not1bit_21_output[0]));
  AND1bit2X1 and1bit2x1_39 (.in_1(not1bit_21_output), .out_2(and1bit2x1_39_out_2[1]));
  AND1bit2X1 and1bit2x1_40 (.in_1({not1bit_21_output[1], in_1[11]}), .out_2(and1bit2x1_6_out_2[6]));
  NOT1bit not1bit_22 (.Input(in_1[10]), .Output(not1bit_22_output[0]));
  AND1bit2X1 and1bit2x1_41 (.in_1({and1bit2x1_39_out_2[1], not1bit_22_output[0]}), .out_2(not1bit_23_output[1]));
  AND1bit2X1 and1bit2x1_42 (.in_1({and1bit2x1_39_out_2[1], in_1[10]}), .out_2(and1bit2x1_6_out_2[5]));
  NOT1bit not1bit_23 (.Input(in_1[9]), .Output(not1bit_23_output[0]));
  AND1bit2X1 and1bit2x1_43 (.in_1(not1bit_23_output), .out_2(not1bit_24_output[1]));
  AND1bit2X1 and1bit2x1_44 (.in_1({not1bit_23_output[1], in_1[9]}), .out_2(and1bit2x1_6_out_2[4]));
  NOT1bit not1bit_24 (.Input(in_1[8]), .Output(not1bit_24_output[0]));
  AND1bit2X1 and1bit2x1_45 (.in_1(not1bit_24_output), .out_2(not1bit_25_output[1]));
  AND1bit2X1 and1bit2x1_46 (.in_1({not1bit_24_output[1], in_1[8]}), .out_2(and1bit2x1_14_out_2[7]));
  NOT1bit not1bit_25 (.Input(in_1[7]), .Output(not1bit_25_output[0]));
  AND1bit2X1 and1bit2x1_47 (.in_1(not1bit_25_output), .out_2(not1bit_26_output[1]));
  AND1bit2X1 and1bit2x1_48 (.in_1({not1bit_25_output[1], in_1[7]}), .out_2(and1bit2x1_16_out_2[3]));
  NOT1bit not1bit_26 (.Input(in_1[6]), .Output(not1bit_26_output[0]));
  AND1bit2X1 and1bit2x1_49 (.in_1(not1bit_26_output), .out_2(not1bit_27_output[1]));
  AND1bit2X1 and1bit2x1_50 (.in_1({not1bit_26_output[1], in_1[6]}), .out_2(and1bit2x1_2_out_2[3]));
  NOT1bit not1bit_27 (.Input(in_1[5]), .Output(not1bit_27_output[0]));
  AND1bit2X1 and1bit2x1_51 (.in_1(not1bit_27_output), .out_2(not1bit_28_output[1]));
  AND1bit2X1 and1bit2x1_52 (.in_1({not1bit_27_output[1], in_1[5]}), .out_2(and1bit2x1_2_out_2[2]));
  NOT1bit not1bit_28 (.Input(in_1[4]), .Output(not1bit_28_output[0]));
  AND1bit2X1 and1bit2x1_53 (.in_1(not1bit_28_output), .out_2(not1bit_29_output[1]));
  AND1bit2X1 and1bit2x1_54 (.in_1({not1bit_28_output[1], in_1[4]}), .out_2(and1bit2x1_6_out_2[3]));
  NOT1bit not1bit_29 (.Input(in_1[3]), .Output(not1bit_29_output[0]));
  AND1bit2X1 and1bit2x1_55 (.in_1(not1bit_29_output), .out_2(not1bit_30_output[1]));
  AND1bit2X1 and1bit2x1_56 (.in_1({not1bit_29_output[1], in_1[3]}), .out_2(and1bit2x1_6_out_2[2]));
  NOT1bit not1bit_30 (.Input(in_1[2]), .Output(not1bit_30_output[0]));
  AND1bit2X1 and1bit2x1_57 (.in_1(not1bit_30_output), .out_2(not1bit_31_output[1]));
  AND1bit2X1 and1bit2x1_58 (.in_1({not1bit_30_output[1], in_1[2]}), .out_2(and1bit2x1_6_out_2[1]));
  NOT1bit not1bit_31 (.Input(in_1[1]), .Output(not1bit_31_output[0]));
  AND1bit2X1 and1bit2x1_59 (.in_1(not1bit_31_output), .out_2(not1bit_32_output[1]));
  AND1bit2X1 and1bit2x1_60 (.in_1({not1bit_31_output[1], in_1[1]}), .out_2(and1bit2x1_6_out_2[0]));
  NOT1bit not1bit_32 (.Input(in_1[0]), .Output(not1bit_32_output[0]));
  AND1bit2X1 and1bit2x1_61 (.in_1(not1bit_32_output), .out_2(and1bit2x1_61_out_2));
  AND1bit2X1 and1bit2x1_62 (.in_1({not1bit_32_output[1], in_1[0]}), .out_2(out_2[5]));
  OR1BIT16X1 or1bit16x1_1 (.in_1(and1bit2x1_6_out_2), .out_2(out_2[2]));
  OR1BIT16X1 or1bit16x1_2 (
    .in_1({and1bit2x1_2_out_2[15:14], and1bit2x1_6_out_2[13:12], and1bit2x1_2_out_2[11:10], and1bit2x1_6_out_2[9:8], and1bit2x1_2_out_2[7:6], and1bit2x1_6_out_2[5:4], and1bit2x1_2_out_2[3:2], and1bit2x1_6_out_2[1:0]}),
    .out_2(out_2[1]));
  OR1BIT16X1 or1bit16x1_3 (
    .in_1({in_1[31], and1bit2x1_2_out_2[14], and1bit2x1_6_out_2[14], and1bit2x1_6_out_2[12], and1bit2x1_16_out_2[11], and1bit2x1_2_out_2[10], and1bit2x1_6_out_2[10], and1bit2x1_6_out_2[8], and1bit2x1_16_out_2[7], and1bit2x1_2_out_2[6], and1bit2x1_6_out_2[6], and1bit2x1_6_out_2[4], and1bit2x1_16_out_2[3], and1bit2x1_2_out_2[2], and1bit2x1_6_out_2[2], and1bit2x1_6_out_2[0]}),
    .out_2(out_2[0]));
  OR1BIT16X1 or1bit16x1_4 (
    .in_1({and1bit2x1_14_out_2[15], and1bit2x1_16_out_2[11], and1bit2x1_2_out_2[11:10], and1bit2x1_6_out_2[11:8], and1bit2x1_14_out_2[7], and1bit2x1_16_out_2[3], and1bit2x1_2_out_2[3:2], and1bit2x1_6_out_2[3:0]}),
    .out_2(out_2[3]));
  OR1BIT16X1 or1bit16x1_5 (
    .in_1({and1bit2x1_30_out_2[15], and1bit2x1_16_out_2[7], and1bit2x1_2_out_2[7:6], and1bit2x1_6_out_2[7:4], and1bit2x1_14_out_2[7], and1bit2x1_16_out_2[3], and1bit2x1_2_out_2[3:2], and1bit2x1_6_out_2[3:0]}),
    .out_2(out_2[4]));

  assign out_2[10:6] = {5{1'b0}};
endmodule

module Control (
  input  [10:0] Ae,
  input  [10:0] Be,
  input  [19:0] Af,
  input  [19:0] Bf,
  output [10:0] Se,
  output [19:0] Sf,
  output C,
  output out_8
);

  wire adder11bit_1_cout, adder20bit_1_cout, or1bit11x1_1_out_2, or1bit20x1_1_out_2;
  wire [0:0] and1bit2x1_1_out_2, not1bit_3_output;
  wire [1:1] not1bit_4_output;
  wire [10:0] adder11bit_1_dataout, not11bit_1_output, xor11bit2x1_1_output;
  wire [10:10] not1bit_1_output;
  wire [19:0] adder20bit_1_dataout, not20bit_1_output, xor20bit2x1_1_output;
  wire [19:19] not1bit_2_output;

  NOT11bit not11bit_1 (.Input(Be), .Output(not11bit_1_output));
  NOT20bit not20bit_1 (.Input(Bf), .Output(not20bit_1_output));
  Adder11bit adder11bit_1 (
    .Data0(Ae), .Data1(not11bit_1_output), .Cin(1'b1), .Cout(adder11bit_1_cout),
    .DataOut(adder11bit_1_dataout));
  NOT1bit not1bit_1 (.Input(adder11bit_1_cout), .Output(not1bit_1_output[10]));
  Adder20bit adder20bit_1 (
    .Data0(Af), .Data1(not20bit_1_output), .Cin(1'b1), .Cout(adder20bit_1_cout),
    .DataOut(adder20bit_1_dataout));
  NOT1bit not1bit_2 (.Input(adder20bit_1_cout), .Output(not1bit_2_output[19]));
  Adder11bit adder11bit_2 (
    .Data0(xor11bit2x1_1_output), .Data1({11{1'b0}}), .Cin(not1bit_1_output[10]), .DataOut(Se));  // open: Cout
  XOR11bit2X1 xor11bit2x1_1 (
    .Input_A(adder11bit_1_dataout), .Input_B({11{not1bit_1_output[10]}}), .Output(xor11bit2x1_1_output));
  XOR20bit2X1 xor20bit2x1_1 (
    .Input_A(adder20bit_1_dataout), .Input_B({20{not1bit_2_output[19]}}), .Output(xor20bit2x1_1_output));
  Adder20bit adder20bit_2 (
    .Data0(xor20bit2x1_1_output), .Data1({20{1'b0}}), .Cin(not1bit_2_output[19]), .DataOut(Sf));  // open: Cout
  OR1BIT11X1 or1bit11x1_1 (.in_1(Se), .out_2(or1bit11x1_1_out_2));
  OR1BIT20X1 or1bit20x1_1 (.in_1(Sf), .out_2(or1bit20x1_1_out_2));
  NOT1bit not1bit_3 (.Input(or1bit11x1_1_out_2), .Output(not1bit_3_output[0]));
  NOT1bit not1bit_4 (.Input(or1bit20x1_1_out_2), .Output(not1bit_4_output[1]));
  AND1bit2X1 and1bit2x1_1 (.in_1({not1bit_2_output[19], not1bit_3_output[0]}), .out_2(and1bit2x1_1_out_2[0]));
  OR1bit2X1 or1bit2x1_1 (.in_1({not1bit_1_output[10], and1bit2x1_1_out_2[0]}), .out_2(C));
  AND1bit2X1 and1bit2x1_2 (.in_1({not1bit_4_output[1], not1bit_3_output[0]}), .out_2(out_8));

  // Notes on the sheet:
  //   out_8: pull=down
endmodule

module Normalizer (
  input  [31:0] Fin,
  input  [10:0] Ein,
  output [31:0] Fout,
  output [10:0] Eout,
  output Underflow
);

  wire adder11bit_1_cout, or1bit11x1_1_out_2;
  wire [1:0] not1bit_1_output;
  wire [10:0] not11bit_1_output, priorityencoder_1_out_2;

  PriorityEncoder priorityencoder_1 (.in_1(Fin), .out_2(priorityencoder_1_out_2));
  NOT11bit not11bit_1 (.Input(priorityencoder_1_out_2), .Output(not11bit_1_output));
  Adder11bit adder11bit_1 (
    .Data0(not11bit_1_output), .Data1(Ein), .Cin(1'b1), .Cout(adder11bit_1_cout), .DataOut(Eout));
  OR1BIT11X1 or1bit11x1_1 (.in_1(Eout), .out_2(or1bit11x1_1_out_2));
  CustomLeftShifter customleftshifter_1 (
    .Shift_bit(1'b0), .Data_in(Fin), .Shift_amount(priorityencoder_1_out_2), .Data_out(Fout));
  NOT1bit not1bit_1 (.Input(adder11bit_1_cout), .Output(not1bit_1_output[0]));
  NOT1bit not1bit_2 (.Input(or1bit11x1_1_out_2), .Output(not1bit_1_output[1]));
  OR1bit2X1 or1bit2x1_1 (.in_1(not1bit_1_output), .out_2(Underflow));
endmodule

module Rounder (
  input  [10:0] E_unrounded,
  input  [31:0] F_unrounded,
  output [10:0] E_rounded,
  output [19:0] F_rounded
);

  wire adder20bit_1_cout, adder23bit_1_cout, adder26bit_1_cout, adder29bit_1_cout, stickyadderbit_1_addbit,
       stickyadderbit_2_addbit, stickyadderbit_3_addbit, stickyadderbit_4_addbit;
  wire [3:0] mux23bit2x1_1_dataout;
  wire [10:0] adder11bit_1_dataout, adder11bit_2_dataout, adder11bit_3_dataout;
  wire [19:0] adder20bit_1_dataout;
  wire [19:1] mux23bit2x1_1_dataout_2;
  wire [22:0] adder23bit_1_dataout;
  wire [25:0] adder26bit_1_dataout, mux26bit2x1_1_dataout;
  wire [28:0] adder29bit_1_dataout, mux29bit2x1_1_dataout;

  StickyAdderBit stickyadderbit_1 (.LGRS(F_unrounded[3:0]), .addBit(stickyadderbit_1_addbit));
  Adder29bit adder29bit_1 (
    .Data0(F_unrounded[31:3]), .Data1({29{1'b0}}), .Cin(stickyadderbit_1_addbit), .Cout(adder29bit_1_cout),
    .DataOut(adder29bit_1_dataout));
  Adder11bit adder11bit_1 (
    .Data0(E_unrounded), .Data1({11{1'b0}}), .Cin(adder29bit_1_cout), .DataOut(adder11bit_1_dataout));  // open: Cout
  MUX29bit2x1 mux29bit2x1_1 (
    .S(adder29bit_1_cout), .Data0(adder29bit_1_dataout), .Data1({29{1'b0}}), .DataOut(mux29bit2x1_1_dataout));
  StickyAdderBit stickyadderbit_2 (.LGRS(mux29bit2x1_1_dataout[3:0]), .addBit(stickyadderbit_2_addbit));
  Adder26bit adder26bit_1 (
    .Data0(mux29bit2x1_1_dataout[28:3]), .Data1({26{1'b0}}), .Cin(stickyadderbit_2_addbit),
    .Cout(adder26bit_1_cout), .DataOut(adder26bit_1_dataout));
  Adder11bit adder11bit_2 (
    .Data0(adder11bit_1_dataout), .Data1({11{1'b0}}), .Cin(adder26bit_1_cout), .DataOut(adder11bit_2_dataout));  // open: Cout
  MUX26bit2x1 mux26bit2x1_1 (
    .S(adder26bit_1_cout), .Data0(adder26bit_1_dataout), .Data1({26{1'b0}}), .DataOut(mux26bit2x1_1_dataout));
  StickyAdderBit stickyadderbit_3 (.LGRS(mux26bit2x1_1_dataout[3:0]), .addBit(stickyadderbit_3_addbit));
  Adder23bit adder23bit_1 (
    .Data0(mux26bit2x1_1_dataout[25:3]), .Data1({23{1'b0}}), .Cin(stickyadderbit_3_addbit),
    .Cout(adder23bit_1_cout), .DataOut(adder23bit_1_dataout));
  Adder11bit adder11bit_3 (
    .Data0(adder11bit_2_dataout), .Data1({11{1'b0}}), .Cin(adder23bit_1_cout), .DataOut(adder11bit_3_dataout));  // open: Cout
  MUX23bit2x1 mux23bit2x1_1 (
    .S(adder23bit_1_cout), .Data0(adder23bit_1_dataout), .Data1({23{1'b0}}),
    .DataOut({mux23bit2x1_1_dataout_2, mux23bit2x1_1_dataout}));
  StickyAdderBit stickyadderbit_4 (.LGRS(mux23bit2x1_1_dataout), .addBit(stickyadderbit_4_addbit));
  Adder11bit adder11bit_4 (
    .Data0(adder11bit_3_dataout), .Data1({11{1'b0}}), .Cin(adder20bit_1_cout), .DataOut(E_rounded));  // open: Cout
  Adder20bit adder20bit_1 (
    .Data0({mux23bit2x1_1_dataout_2, mux23bit2x1_1_dataout[3]}), .Data1({20{1'b0}}),
    .Cin(stickyadderbit_4_addbit), .Cout(adder20bit_1_cout), .DataOut(adder20bit_1_dataout));
  MUX20bit2x1 mux20bit2x1_1 (
    .S(adder20bit_1_cout), .Data0(adder20bit_1_dataout), .Data1({20{1'b0}}), .DataOut(F_rounded));
endmodule

// FPA
module FloatingPointAdder (
  input  [31:0] A,
  input  [31:0] B,
  output [31:0] F,
  output Underflow,
  output Overflow
);

  wire and1bit1x1_1_out_3, and1bit2x1_1_out_2, and1bit2x1_2_out_2, control_1_c, incrementexponent_2_overflow,
       inputsplitter_1_s1, inputsplitter_2_s1, mux1bit2x1_1_dataout, mux1bit2x1_2_dataout,
       normalizer_1_underflow, not1bit_1_output, not1bit_3_output, not1bit_5_output, or1bit11x1_1_out_2;
  wire [1:0] not1bit_2_output, not1bit_4_output, xor1bit2x1_1_output;
  wire [10:0] control_1_se, incrementexponent_1_a_1, inputsplitter_1_e11, inputsplitter_2_e11,
       inputsplitter_3_e11, mux11bit2x1_1_dataout, mux11bit2x1_2_dataout, normalizer_1_eout,
       rounder_1_e_rounded;
  wire [19:0] inputsplitter_1_f20, inputsplitter_2_f20, mux20bit2x1_1_dataout, mux20bit2x1_2_dataout,
       rounder_1_f_rounded;
  wire [31:0] adder32bit_1_dataout, customrightshifter_1_data_out, makesignificand_1_out32,
       makesignificand_2_out32, mux32bit2x1_1_dataout, normalizer_1_fout, outputsplitter_1__32,
       selectinverse_1_dataout, zero32bit_1_out_1;

  InputSplitter inputsplitter_1 (
    ._32(A), .s1(inputsplitter_1_s1), .e11(inputsplitter_1_e11), .f20(inputsplitter_1_f20));
  InputSplitter inputsplitter_2 (
    ._32(B), .s1(inputsplitter_2_s1), .e11(inputsplitter_2_e11), .f20(inputsplitter_2_f20));
  MUX1bit2x1 mux1bit2x1_1 (
    .S(control_1_c), .Data0(inputsplitter_1_s1), .Data1(inputsplitter_2_s1), .DataOut(mux1bit2x1_1_dataout));
  MUX1bit2x1 mux1bit2x1_2 (
    .S(not1bit_1_output), .Data0(inputsplitter_1_s1), .Data1(inputsplitter_2_s1),
    .DataOut(mux1bit2x1_2_dataout));
  MUX11bit2x1 mux11bit2x1_1 (
    .S(control_1_c), .Data0(inputsplitter_1_e11), .Data1(inputsplitter_2_e11), .DataOut(mux11bit2x1_1_dataout));
  IncrementExponent incrementexponent_1 (.A(mux11bit2x1_1_dataout), .A_1(incrementexponent_1_a_1));  // open: Overflow
  MUX20bit2x1 mux20bit2x1_1 (
    .S(control_1_c), .Data0(inputsplitter_1_f20), .Data1(inputsplitter_2_f20), .DataOut(mux20bit2x1_1_dataout));
  makeSignificand makesignificand_1 (.in20(mux20bit2x1_1_dataout), .out32(makesignificand_1_out32));
  makeSignificand makesignificand_2 (.in20(mux20bit2x1_2_dataout), .out32(makesignificand_2_out32));
  MUX20bit2x1 mux20bit2x1_2 (
    .S(not1bit_1_output), .Data0(inputsplitter_1_f20), .Data1(inputsplitter_2_f20),
    .DataOut(mux20bit2x1_2_dataout));
  NOT1bit not1bit_1 (.Input(control_1_c), .Output(not1bit_1_output));
  Control control_1 (
    .Ae(inputsplitter_1_e11), .Be(inputsplitter_2_e11), .Af(inputsplitter_1_f20), .Bf(inputsplitter_2_f20),
    .Se(control_1_se), .C(control_1_c), .out_8(xor1bit2x1_1_output[1]));  // open: Sf
  XOR1bit2X1 xor1bit2x1_1 (
    .Input_A(mux1bit2x1_1_dataout), .Input_B(mux1bit2x1_2_dataout), .Output(xor1bit2x1_1_output[0]));
  NOT1bit not1bit_2 (.Input(xor1bit2x1_1_output[0]), .Output(not1bit_2_output[0]));
  CustomRightShifter customrightshifter_1 (
    .Shift_bit(1'b0), .Data_in(makesignificand_2_out32), .Shift_amount(control_1_se),
    .Data_out(customrightshifter_1_data_out));
  SelectInverse selectinverse_1 (
    .Data_in(customrightshifter_1_data_out), .Selector(xor1bit2x1_1_output[0]),
    .DataOut(selectinverse_1_dataout));
  AND1bit2X1 and1bit2x1_1 (.in_1(not1bit_2_output), .out_2(and1bit2x1_1_out_2));
  Adder32bit adder32bit_1 (
    .Data0(makesignificand_1_out32), .Data1(selectinverse_1_dataout), .Cin(xor1bit2x1_1_output[0]),
    .Cout(not1bit_2_output[1]), .DataOut(adder32bit_1_dataout));
  AND1bit2X1 and1bit2x1_2 (.in_1(xor1bit2x1_1_output), .out_2(and1bit2x1_2_out_2));
  Normalizer normalizer_1 (
    .Fin(adder32bit_1_dataout), .Ein(incrementexponent_1_a_1), .Fout(normalizer_1_fout),
    .Eout(normalizer_1_eout), .Underflow(normalizer_1_underflow));
  NOT1bit not1bit_3 (.Input(and1bit2x1_1_out_2), .Output(not1bit_3_output));
  MUX11bit2x1 mux11bit2x1_2 (
    .S(and1bit2x1_1_out_2), .Data0(normalizer_1_eout), .Data1(incrementexponent_1_a_1),
    .DataOut(mux11bit2x1_2_dataout));
  Rounder rounder_1 (
    .E_unrounded(mux11bit2x1_2_dataout), .F_unrounded(mux32bit2x1_1_dataout),
    .E_rounded(rounder_1_e_rounded), .F_rounded(rounder_1_f_rounded));
  MUX32bit2x1 mux32bit2x1_1 (
    .S(and1bit2x1_1_out_2), .Data0(normalizer_1_fout), .Data1(adder32bit_1_dataout),
    .DataOut(mux32bit2x1_1_dataout));
  InputSplitter inputsplitter_3 (._32(F), .e11(inputsplitter_3_e11));  // open: s1, f20
  OR1BIT11X1 or1bit11x1_1 (.in_1(inputsplitter_3_e11), .out_2(or1bit11x1_1_out_2));
  AND1bit1X1 and1bit1x1_1 (.in_1(normalizer_1_underflow), .in_2(not1bit_3_output), .out_3(and1bit1x1_1_out_3));
  OutputSplitter outputsplitter_1 (
    ._1(mux1bit2x1_1_dataout), ._11(rounder_1_e_rounded), ._20(rounder_1_f_rounded),
    ._32(outputsplitter_1__32));
  ZERO32bit zero32bit_1 (.out_1(zero32bit_1_out_1));
  NOT1bit not1bit_4 (.Input(or1bit11x1_1_out_2), .Output(not1bit_4_output[0]));
  IncrementExponent incrementexponent_2 (
    .A(rounder_1_e_rounded), .Overflow(incrementexponent_2_overflow));  // open: A_1
  NOT1bit not1bit_5 (.Input(and1bit1x1_1_out_3), .Output(not1bit_5_output));
  MUX32bit2x1 mux32bit2x1_2 (
    .S(and1bit2x1_2_out_2), .Data0(outputsplitter_1__32), .Data1(zero32bit_1_out_1), .DataOut(F));
  OR1bit2X1 or1bit2x1_1 (.in_1(not1bit_4_output), .out_2(Underflow));
  AND1bit1X1 and1bit1x1_2 (.in_1(incrementexponent_2_overflow), .in_2(not1bit_5_output), .out_3(Overflow));
  MUX1bit2x1 mux1bit2x1_3 (
    .S(and1bit2x1_1_out_2), .Data0(normalizer_1_underflow), .Data1(1'b0), .DataOut(not1bit_4_output[1]));
endmodule

module main (
  input  [31:0] in_1,
  input  [31:0] in_2,
  output [31:0] out_3,
  output Underflow,
  output Overflow
);

  FloatingPointAdder floatingpointadder_1 (.A(in_1), .B(in_2), .F(out_3), .Underflow(Underflow), .Overflow(Overflow));
endmodule
